// Logisim project ALU.circ as structural Verilog: 25 circuits, main circuit ALU
module ALU (
  input  [5:0] X,
  input  [4:0] Input,
  input  [5:0] Y,
  output [5:0] Answer,
  output ZF,
  output BAF,
  output INV_OP
);

  wire [8:0] ADD_s0, AND_s0, CMPZ_s0, DEC_s0, DIV_z0, INC_s0, INV_x0, MUL_z0, N0_s0, N1_s0, NEG_s0, NOT_s0,
       OP1_s0, OP2_s0, OP3_s0, OR_s0, ROL_s0, ROR_s0, SHL_s0, SHR_s0, SUB_s0, VLD_s0, XOR_s0;
  wire [8:8] multiplexer_1_out;

  VLD VLD (
    .b0(X[5]), .b1(X[4]), .b2(X[3]), .b3(X[2]), .b4(X[1]), .b5(X[0]), .s0(VLD_s0[0]), .s1(VLD_s0[1]),
    .s2(VLD_s0[2]), .s3(VLD_s0[3]), .s4(VLD_s0[4]), .s5(VLD_s0[5]), .ZF(VLD_s0[6]), .BAF(VLD_s0[7]),
    .INV_OP(VLD_s0[8]));
  NEG NEG (
    .b0(X[5]), .b1(X[4]), .b2(X[3]), .b3(X[2]), .b4(X[1]), .b5(X[0]), .s0(NEG_s0[0]), .s1(NEG_s0[1]),
    .s2(NEG_s0[2]), .s3(NEG_s0[3]), .s4(NEG_s0[4]), .s5(NEG_s0[5]), .ZF(NEG_s0[6]), .BAF(NEG_s0[7]),
    .INV_OP(NEG_s0[8]));
  INC INC (
    .b0(X[5]), .b1(X[4]), .b2(X[3]), .b3(X[2]), .b4(X[1]), .b5(X[0]), .s0(INC_s0[0]), .s1(INC_s0[1]),
    .s2(INC_s0[2]), .s3(INC_s0[3]), .s4(INC_s0[4]), .s5(INC_s0[5]), .ZF(INC_s0[6]), .BAF(INC_s0[7]),
    .INV_OP(INC_s0[8]));
  DEC DEC (
    .b0(X[5]), .b1(X[4]), .b2(X[3]), .b3(X[2]), .b4(X[1]), .b5(X[0]), .s0(DEC_s0[0]), .s1(DEC_s0[1]),
    .s2(DEC_s0[2]), .s3(DEC_s0[3]), .s4(DEC_s0[4]), .s5(DEC_s0[5]), .ZF(DEC_s0[6]), .BAF(DEC_s0[7]),
    .INV_OP(DEC_s0[8]));
  CMPZ CMPZ (
    .b0(X[5]), .b1(X[4]), .b2(X[3]), .b3(X[2]), .b4(X[1]), .b5(X[0]), .INV_OP(CMPZ_s0[8]), .s0(CMPZ_s0[0]),
    .s1(CMPZ_s0[1]), .s2(CMPZ_s0[2]), .s3(CMPZ_s0[3]), .s4(CMPZ_s0[4]), .s5(CMPZ_s0[5]), .ZF(CMPZ_s0[6]),
    .BAF(CMPZ_s0[7]));
  INV INV (
    .b0(X[5]), .b1(X[4]), .b2(X[3]), .b3(X[2]), .b4(X[1]), .b5(X[0]), .x0(INV_x0[0]), .x1(INV_x0[1]),
    .x2(INV_x0[2]), .x3(INV_x0[3]), .x4(INV_x0[4]), .x5(INV_x0[5]), .ZF(INV_x0[6]), .BAF(INV_x0[7]),
    .INV_OP(INV_x0[8]));
  SHL SHL (
    .b0(X[5]), .b1(X[4]), .b2(X[3]), .b3(X[2]), .b4(X[1]), .b5(X[0]), .s0(SHL_s0[0]), .s1(SHL_s0[1]),
    .s2(SHL_s0[2]), .s3(SHL_s0[3]), .s4(SHL_s0[4]), .s5(SHL_s0[5]), .ZF(SHL_s0[6]), .BAF(SHL_s0[7]),
    .INV_OP(SHL_s0[8]));
  SHR SHR (
    .b0(X[5]), .b1(X[4]), .b2(X[3]), .b3(X[2]), .b4(X[1]), .b5(X[0]), .s0(SHR_s0[0]), .s1(SHR_s0[1]),
    .s2(SHR_s0[2]), .s3(SHR_s0[3]), .s4(SHR_s0[4]), .s5(SHR_s0[5]), .ZF(SHR_s0[6]), .BAF(SHR_s0[7]),
    .INV_OP(SHR_s0[8]));
  ROL ROL (
    .b0(X[5]), .b1(X[4]), .b2(X[3]), .b3(X[2]), .b4(X[1]), .b5(X[0]), .s0(ROL_s0[0]), .s1(ROL_s0[1]),
    .s2(ROL_s0[2]), .s3(ROL_s0[3]), .s4(ROL_s0[4]), .s5(ROL_s0[5]), .ZF(ROL_s0[6]), .BAF(ROL_s0[7]),
    .INV_OP(ROL_s0[8]));
  ROR ROR (
    .b0(X[5]), .b1(X[4]), .b2(X[3]), .b3(X[2]), .b4(X[1]), .b5(X[0]), .s0(ROR_s0[0]), .s1(ROR_s0[1]),
    .s2(ROR_s0[2]), .s3(ROR_s0[3]), .s4(ROR_s0[4]), .s5(ROR_s0[5]), .ZF(ROR_s0[6]), .BAF(ROR_s0[7]),
    .INV_OP(ROR_s0[8]));
  NOT NOT (
    .b0(X[5]), .b1(X[4]), .b2(X[3]), .b3(X[2]), .b4(X[1]), .b5(X[0]), .s0(NOT_s0[0]), .s1(NOT_s0[1]),
    .s2(NOT_s0[2]), .s3(NOT_s0[3]), .s4(NOT_s0[4]), .s5(NOT_s0[5]), .ZF(NOT_s0[6]), .BAF(NOT_s0[7]),
    .INV_OP(NOT_s0[8]));
  N1 N1 (
    .b0(X[5]), .b1(X[4]), .b2(X[3]), .b3(X[2]), .b4(X[1]), .b5(X[0]), .s0(N1_s0[0]), .s1(N1_s0[1]),
    .s2(N1_s0[2]), .s3(N1_s0[3]), .s4(N1_s0[4]), .s5(N1_s0[5]), .ZF(N1_s0[6]), .BAF(N1_s0[7]),
    .INV_OP(N1_s0[8]));
  N0 N0 (
    .b0(X[5]), .b1(X[4]), .b2(X[3]), .b3(X[2]), .b4(X[1]), .b5(X[0]), .s0(N0_s0[0]), .s1(N0_s0[1]),
    .s2(N0_s0[2]), .s3(N0_s0[3]), .s4(N0_s0[4]), .s5(N0_s0[5]), .ZF(N0_s0[6]), .BAF(N0_s0[7]),
    .INV_OP(N0_s0[8]));
  ADD ADD (
    .x0(X[5]), .x1(X[4]), .x2(X[3]), .x3(X[2]), .x4(X[1]), .x5(X[0]), .b0(Y[5]), .b1(Y[4]), .b2(Y[3]),
    .b3(Y[2]), .b4(Y[1]), .b5(Y[0]), .s0(ADD_s0[0]), .s1(ADD_s0[1]), .s2(ADD_s0[2]), .s3(ADD_s0[3]),
    .s4(ADD_s0[4]), .s5(ADD_s0[5]), .ZF(ADD_s0[6]), .BAF(ADD_s0[7]), .INV_OP(ADD_s0[8]));  // open: out_20
  SUB SUB (
    .x0(X[5]), .x1(X[4]), .x2(X[3]), .x3(X[2]), .x4(X[1]), .x5(X[0]), .b0(Y[5]), .b1(Y[4]), .b2(Y[3]),
    .b3(Y[2]), .b4(Y[1]), .b5(Y[0]), .s0(SUB_s0[0]), .s1(SUB_s0[1]), .s2(SUB_s0[2]), .s3(SUB_s0[3]),
    .s4(SUB_s0[4]), .s5(SUB_s0[5]), .ZF(SUB_s0[6]), .BAF(SUB_s0[7]), .INV_OP(SUB_s0[8]));  // open: out_21, out_13
  MUL MUL (
    .x0(X[5]), .x1(X[4]), .x2(X[3]), .x3(X[2]), .x4(X[1]), .x5(X[0]), .b0(Y[5]), .b1(Y[4]), .b2(Y[3]),
    .b3(Y[2]), .b4(Y[1]), .b5(Y[0]), .ZF(MUL_z0[6]), .z0(MUL_z0[0]), .z1(MUL_z0[1]), .z2(MUL_z0[2]),
    .z3(MUL_z0[3]), .z4(MUL_z0[4]), .z5(MUL_z0[5]), .BAF(MUL_z0[7]), .INV_OP(MUL_z0[8]));
  DIV DIV (
    .x0(X[5]), .x1(X[4]), .x2(X[3]), .x3(X[2]), .x4(X[1]), .x5(X[0]), .b0(Y[5]), .b1(Y[4]), .b2(Y[3]),
    .b3(Y[2]), .b4(Y[1]), .ZF(DIV_z0[6]), .b5(Y[0]), .z0(DIV_z0[0]), .z1(DIV_z0[1]), .z2(DIV_z0[2]),
    .z3(DIV_z0[3]), .z4(DIV_z0[4]), .z5(DIV_z0[5]), .BAF(DIV_z0[7]), .INV_OP(DIV_z0[8]));  // open: out_13
  OP1 OP1 (
    .x0(X[5]), .x1(X[4]), .x2(X[3]), .x3(X[2]), .x4(X[1]), .x5(X[0]), .b0(Y[5]), .b1(Y[4]), .b2(Y[3]),
    .b3(Y[2]), .b4(Y[1]), .b5(Y[0]), .BAF(OP1_s0[7]), .s0(OP1_s0[0]), .s1(OP1_s0[1]), .s2(OP1_s0[2]),
    .s3(OP1_s0[3]), .s4(OP1_s0[4]), .ZF(OP1_s0[6]), .INV_OP(OP1_s0[8]), .s5(OP1_s0[5]));  // open: out_15, out_13
  OP2 OP2 (
    .b0(X[5]), .b1(X[4]), .b2(X[3]), .b3(X[2]), .b4(X[1]), .b5(X[0]), .x0(Y[5]), .x1(Y[4]), .x2(Y[3]),
    .x3(Y[2]), .x4(Y[1]), .x5(Y[0]), .BAF(OP2_s0[7]), .s5(OP2_s0[5]), .s0(OP2_s0[0]), .s1(OP2_s0[1]),
    .s2(OP2_s0[2]), .s3(OP2_s0[3]), .s4(OP2_s0[4]), .ZF(OP2_s0[6]), .INV_OP(OP2_s0[8]));
  OP3 OP3 (
    .b0(X[5]), .b1(X[4]), .b2(X[3]), .b3(X[2]), .b4(X[1]), .b5(X[0]), .s0(OP3_s0[0]), .s1(OP3_s0[1]),
    .s2(OP3_s0[2]), .s3(OP3_s0[3]), .s4(OP3_s0[4]), .s5(OP3_s0[5]), .ZF(OP3_s0[6]), .BAF(OP3_s0[7]),
    .INV_OP(OP3_s0[8]));
  XOR XOR (
    .b0(X[5]), .b1(X[4]), .b2(X[3]), .b3(X[2]), .b4(X[1]), .b5(X[0]), .x0(Y[5]), .x1(Y[4]), .x2(Y[3]),
    .x3(Y[2]), .x4(Y[1]), .x5(Y[0]), .BAF(XOR_s0[7]), .s0(XOR_s0[0]), .s1(XOR_s0[1]), .s2(XOR_s0[2]),
    .s3(XOR_s0[3]), .s4(XOR_s0[4]), .s5(XOR_s0[5]), .ZF(XOR_s0[6]), .INV_OP(XOR_s0[8]));
  AND AND (
    .b0(X[5]), .b1(X[4]), .b2(X[3]), .b3(X[2]), .b4(X[1]), .b5(X[0]), .x0(Y[5]), .x1(Y[4]), .x2(Y[3]),
    .x3(Y[2]), .x4(Y[1]), .x5(Y[0]), .BAF(AND_s0[7]), .s0(AND_s0[0]), .s1(AND_s0[1]), .s2(AND_s0[2]),
    .s3(AND_s0[3]), .s4(AND_s0[4]), .s5(AND_s0[5]), .ZF(AND_s0[6]), .INV_OP(AND_s0[8]));
  OR OR (
    .b0(X[5]), .b1(X[4]), .b2(X[3]), .b3(X[2]), .b4(X[1]), .b5(X[0]), .x0(Y[5]), .x1(Y[4]), .x2(Y[3]),
    .x3(Y[2]), .x4(Y[1]), .x5(Y[0]), .BAF(OR_s0[7]), .s0(OR_s0[0]), .s1(OR_s0[1]), .s2(OR_s0[2]),
    .s3(OR_s0[3]), .s4(OR_s0[4]), .s5(OR_s0[5]), .ZF(OR_s0[6]), .INV_OP(OR_s0[8]));
  Multiplexer #(.select(5), .width(9)) multiplexer_1 (
    .in0({9{1'b0}}), .in1(VLD_s0), .in2(NEG_s0), .in3(INC_s0), .in4(DEC_s0), .in5(CMPZ_s0), .in6(INV_x0),
    .in7({9{1'b0}}), .in8(SHL_s0), .in9(SHR_s0), .in10(ROL_s0), .in11(ROR_s0), .in12(NOT_s0), .in13(N1_s0),
    .in14(N0_s0), .in15({9{1'b0}}), .in16(ADD_s0), .in17(SUB_s0), .in18(MUL_z0), .in19(DIV_z0),
    .in20({9{1'b0}}), .in21({9{1'b0}}), .in22({9{1'b0}}), .in23({9{1'b0}}), .in24(OP1_s0), .in25(OP2_s0),
    .in26(OP3_s0), .in27({9{1'b0}}), .in28(XOR_s0), .in29(AND_s0), .in30(OR_s0), .in31({9{1'b0}}),
    .out({multiplexer_1_out[8], BAF, ZF, Answer[0], Answer[1], Answer[2], Answer[3], Answer[4], Answer[5]}),
    .sel(Input), .en(1'b1));
  not not_2 (INV_OP, multiplexer_1_out[8]);

  // Notes on the sheet:
  //   000 001
  //   000 010
  //   000 011
  //   000 100
  //   000 101
  //   000 110
  //   001 000
  //   001 001
  //   001 010
  //   001 011
  //   001100
  //   001101
  //   001110
  //   010000
  //   010001
  //   Command
  //   00000 - None
  //   00001 - VLD
  //   00010 - NEG
  //   00011 - INC
  //   00100 - DEC
  //   00101 - CMPZ
  //   00110 - INV
  //   00111 - None
  //   01000 - SHL
  //   01001 - SHR
  //   01010 - ROL
  //   01011 - ROR
  //   01100 - NOT
  //   01101 - N1
  //   01110 - N0
  //   01111 - None
  //   10000 - ADD
  //   10001 - SUB
  //   10010 - MUL
  //   10011 - DIV
  //   10100 - None
  //   10101 - None
  //   10110 - None
  //   10111 - None
  //   11000 - OP1
  //   11001 - OP2
  //   11010 - OP3
  //   11011 - None
  //   11100 - XOR
  //   11101 - AND
  //   11110 - OR
  //   11111 - None
endmodule

module VLD (
  input  b0,
  input  b1,
  input  b2,
  input  b3,
  input  b4,
  input  b5,
  output s0,
  output s1,
  output s2,
  output s3,
  output s4,
  output s5,
  output ZF,
  output BAF,
  output INV_OP
);

  wire and_1_out, and_2_out, not_1_out, not_2_out, not_3_out, not_4_out, not_5_out, not_6_out, not_7_out;

  not not_1 (not_1_out, b1);
  not not_2 (not_2_out, b2);
  not not_3 (not_3_out, b3);
  not not_4 (not_4_out, b1);
  not not_5 (not_5_out, b2);
  not not_6 (not_6_out, b4);
  not not_7 (not_7_out, b0);
  and and_1 (and_1_out, not_1_out, not_2_out, not_3_out);
  and and_2 (and_2_out, not_4_out, not_5_out, not_6_out);
  or or_1 (s5, not_7_out, and_1_out, and_2_out);

  assign BAF = 1'b0;
  assign INV_OP = 1'b1;
  assign s0 = 1'b0;
  assign s1 = 1'b0;
  assign s2 = 1'b0;
  assign s3 = 1'b0;
  assign s4 = 1'b0;
  assign ZF = 1'b0;
endmodule

module ADD (
  input  x0,
  input  x1,
  input  x2,
  input  x3,
  input  x4,
  input  x5,
  input  b0,
  input  b1,
  input  b2,
  input  b3,
  input  b4,
  input  b5,
  output s0,
  output s1,
  output s2,
  output s3,
  output s4,
  output s5,
  output ZF,
  output [6:0] out_20,
  output BAF,
  output INV_OP
);

  wire not_1_out, not_2_out, not_3_out, not_4_out, not_5_out, not_6_out, not_7_out, not_8_out, VLD_2_s5,
       VLD_s5;
  wire [6:0] adder_1_out;

  VLD VLD (
    .b0(x0), .b1(x1), .b2(x2), .b3(x3), .b4(x4), .b5(x5), .s5(VLD_s5));  // open: s0, s1, s2, s3, s4, ZF, BAF, INV_OP
  VLD VLD_2 (
    .b0(b0), .b1(b1), .b2(b2), .b3(b3), .b4(b4), .b5(b5), .s5(VLD_2_s5));  // open: s0, s1, s2, s3, s4, ZF, BAF, INV_OP
  not not_1 (not_1_out, VLD_s5);
  not not_2 (not_2_out, VLD_2_s5);
  or or_1 (BAF, not_1_out, not_2_out);
  Adder #(.width(6)) adder_1 (
    .a({x0, x1, x2, x3, x4, x5}), .b({b0, b1, b2, b3, b4, b5}), .out(adder_1_out[5:0]), .cout(adder_1_out[6]));  // open: cin
  Divider #(.width(7)) divider_1 (.a(adder_1_out), .b(7'b0100110), .rem(out_20));  // open: out, upper
  not not_3 (not_3_out, out_20[5]);
  not not_4 (not_4_out, out_20[4]);
  not not_5 (not_5_out, out_20[3]);
  not not_6 (not_6_out, out_20[2]);
  not not_7 (not_7_out, out_20[1]);
  not not_8 (not_8_out, out_20[0]);
  and and_1 (ZF, not_3_out, not_4_out, not_5_out, not_6_out, not_7_out, not_8_out);

  assign INV_OP = 1'b1;
  assign s0 = out_20[5];
  assign s1 = out_20[4];
  assign s2 = out_20[3];
  assign s3 = out_20[2];
  assign s4 = out_20[1];
  assign s5 = out_20[0];
endmodule

module NEG (
  input  b0,
  input  b1,
  input  b2,
  input  b3,
  input  b4,
  input  b5,
  output s0,
  output s1,
  output s2,
  output s3,
  output s4,
  output s5,
  output ZF,
  output BAF,
  output INV_OP
);

  wire and_1_out, and_2_out, and_3_out, and_4_out, and_5_out, and_6_out, and_7_out, and_8_out, and_9_out,
       and_10_out, and_11_out, and_12_out, and_13_out, and_14_out, and_15_out, and_16_out, and_17_out,
       and_18_out, and_19_out, and_20_out, and_21_out, and_22_out, and_23_out, and_24_out, and_25_out,
       and_26_out, and_27_out, not_1_out, not_2_out, not_3_out, not_4_out, not_5_out, not_6_out, not_7_out,
       not_8_out, not_9_out, not_10_out, not_11_out, not_12_out, not_13_out, not_14_out, not_15_out,
       not_16_out, not_17_out, not_18_out, not_19_out, not_20_out, not_21_out, not_22_out, not_23_out,
       not_24_out, not_25_out, not_26_out, not_27_out, not_28_out, not_29_out, not_30_out, not_31_out,
       not_32_out, not_33_out, not_34_out, not_35_out, not_36_out, not_37_out, not_38_out, not_39_out,
       not_40_out, not_41_out, not_42_out, not_43_out, not_44_out, not_45_out, not_46_out, not_47_out,
       not_48_out, not_49_out, not_50_out, not_51_out, not_52_out, not_53_out, not_54_out, not_55_out,
       not_56_out, not_57_out, not_58_out, not_59_out, not_60_out, not_61_out, not_62_out, not_63_out,
       not_64_out, not_65_out, not_66_out, not_67_out, not_68_out, not_69_out;

  not not_1 (not_1_out, b0);
  not not_2 (not_2_out, b1);
  not not_3 (not_3_out, b2);
  not not_4 (not_4_out, b3);
  not not_5 (not_5_out, b0);
  not not_6 (not_6_out, b1);
  not not_7 (not_7_out, b2);
  not not_8 (not_8_out, b4);
  not not_9 (not_9_out, b0);
  not not_10 (not_10_out, b1);
  not not_11 (not_11_out, b2);
  not not_12 (not_12_out, b5);
  not not_13 (not_13_out, b0);
  not not_14 (not_14_out, b1);
  not not_15 (not_15_out, b0);
  not not_16 (not_16_out, b1);
  not not_17 (not_17_out, b0);
  not not_18 (not_18_out, b2);
  not not_19 (not_19_out, b3);
  not not_20 (not_20_out, b0);
  not not_21 (not_21_out, b2);
  not not_22 (not_22_out, b4);
  not not_23 (not_23_out, b0);
  not not_24 (not_24_out, b2);
  not not_25 (not_25_out, b5);
  not not_26 (not_26_out, b0);
  not not_27 (not_27_out, b2);
  not not_28 (not_28_out, b0);
  not not_29 (not_29_out, b3);
  not not_30 (not_30_out, b0);
  not not_31 (not_31_out, b4);
  not not_32 (not_32_out, b0);
  not not_33 (not_33_out, b5);
  not not_34 (not_34_out, b0);
  not not_35 (not_35_out, b3);
  not not_36 (not_36_out, b4);
  not not_37 (not_37_out, b0);
  not not_38 (not_38_out, b3);
  not not_39 (not_39_out, b5);
  not not_40 (not_40_out, b1);
  not not_41 (not_41_out, b2);
  not not_42 (not_42_out, b3);
  not not_43 (not_43_out, b4);
  not not_44 (not_44_out, b1);
  not not_45 (not_45_out, b2);
  not not_46 (not_46_out, b3);
  not not_47 (not_47_out, b5);
  not not_48 (not_48_out, b0);
  not not_49 (not_49_out, b0);
  not not_50 (not_50_out, b4);
  not not_51 (not_51_out, b5);
  not not_52 (not_52_out, b1);
  not not_53 (not_53_out, b2);
  not not_54 (not_54_out, b4);
  not not_55 (not_55_out, b5);
  not not_56 (not_56_out, b0);
  not not_57 (not_57_out, b1);
  not not_58 (not_58_out, b2);
  not not_59 (not_59_out, b3);
  not not_60 (not_60_out, b0);
  not not_61 (not_61_out, b1);
  not not_62 (not_62_out, b2);
  not not_63 (not_63_out, b3);
  not not_64 (not_64_out, b1);
  not not_65 (not_65_out, b2);
  not not_66 (not_66_out, b4);
  not not_67 (not_67_out, b1);
  not not_68 (not_68_out, b2);
  not not_69 (not_69_out, b5);
  and and_1 (and_1_out, b0, b3, b4);
  and and_2 (and_2_out, b0, b2);
  and and_3 (and_3_out, b0, b1);
  and and_4 (and_4_out, not_1_out, not_2_out, not_3_out, not_4_out);
  and and_5 (and_5_out, not_5_out, not_6_out, not_7_out, not_8_out);
  and and_6 (and_6_out, not_9_out, not_10_out, not_11_out, not_12_out);
  and and_7 (and_7_out, not_13_out, not_14_out, b3, b4, b5);
  and and_8 (and_8_out, not_15_out, not_16_out, b2);
  and and_9 (and_9_out, not_17_out, b1, not_18_out, not_19_out);
  and and_10 (and_10_out, not_20_out, b1, not_21_out, not_22_out);
  and and_11 (and_11_out, not_23_out, b1, not_24_out, not_25_out);
  and and_12 (and_12_out, not_26_out, not_27_out, b3, b4, b5);
  and and_13 (and_13_out, not_28_out, b2, not_29_out);
  and and_14 (and_14_out, not_30_out, b2, not_31_out);
  and and_15 (and_15_out, not_32_out, b2, not_33_out);
  and and_16 (and_16_out, not_34_out, not_35_out, not_36_out);
  and and_17 (and_17_out, not_37_out, not_38_out, not_39_out);
  and and_18 (and_18_out, not_40_out, not_41_out, not_42_out, not_43_out);
  and and_19 (and_19_out, not_44_out, not_45_out, not_46_out, not_47_out);
  and and_20 (and_20_out, not_48_out, b3, b4, b5);
  and and_21 (and_21_out, not_49_out, not_50_out, not_51_out);
  and and_22 (and_22_out, not_52_out, not_53_out, not_54_out, not_55_out);
  and and_23 (and_23_out, not_56_out, b4, b5);
  and and_24 (and_24_out, not_57_out, not_58_out, not_59_out, b4, b5);
  and and_25 (and_25_out, not_60_out, b5);
  and and_26 (and_26_out, not_61_out, not_62_out, not_63_out, b5);
  and and_27 (and_27_out, not_64_out, not_65_out, not_66_out, b5);
  and and_28 (ZF, b0, not_67_out, not_68_out, b3, b4, not_69_out);
  or or_1 (BAF, and_1_out, and_2_out, and_3_out);
  or or_2 (s0, and_4_out, and_5_out, and_6_out);
  or or_3 (s1, and_7_out, and_8_out, and_9_out, and_10_out, and_11_out);
  or or_4 (s2, and_12_out, and_13_out, and_14_out, and_15_out);
  or or_5 (s3, and_16_out, and_17_out, and_18_out, and_19_out, and_20_out);
  or or_6 (s4, and_21_out, and_22_out, and_23_out, and_24_out);
  or or_7 (s5, and_25_out, and_26_out, and_27_out);

  assign INV_OP = 1'b1;
endmodule

module INC (
  input  b0,
  input  b1,
  input  b2,
  input  b3,
  input  b4,
  input  b5,
  output s0,
  output s1,
  output s2,
  output s3,
  output s4,
  output s5,
  output ZF,
  output BAF,
  output INV_OP
);

  wire and_1_out, and_2_out, and_3_out, and_4_out, and_5_out, and_6_out, and_7_out, and_8_out, and_9_out,
       and_10_out, and_11_out, and_12_out, and_13_out, and_14_out, and_15_out, and_16_out, and_17_out,
       and_18_out, and_19_out, and_20_out, and_21_out, and_22_out, and_23_out, and_24_out, and_25_out,
       and_26_out, and_27_out, not_1_out, not_2_out, not_3_out, not_4_out, not_5_out, not_6_out, not_7_out,
       not_8_out, not_9_out, not_10_out, not_11_out, not_12_out, not_13_out, not_14_out, not_15_out,
       not_16_out, not_17_out, not_18_out, not_19_out, not_20_out, not_21_out, not_22_out, not_23_out,
       not_24_out, not_25_out, not_26_out, not_27_out, not_28_out, not_29_out, not_30_out, not_31_out,
       not_32_out, not_33_out, not_34_out, not_35_out, not_36_out, not_37_out, not_38_out, not_39_out,
       not_40_out, not_41_out, not_42_out, not_43_out, not_44_out, not_45_out, not_46_out, not_47_out,
       not_48_out, not_49_out, not_50_out, not_51_out, not_52_out, not_53_out, not_54_out, not_55_out,
       not_56_out, not_57_out, not_58_out, not_59_out, not_60_out, not_61_out, not_62_out, not_63_out,
       not_64_out;

  not not_1 (not_1_out, b0);
  not not_2 (not_2_out, b1);
  not not_3 (not_3_out, b2);
  not not_4 (not_4_out, b3);
  not not_5 (not_5_out, b1);
  not not_6 (not_6_out, b2);
  not not_7 (not_7_out, b4);
  not not_8 (not_8_out, b5);
  not not_9 (not_9_out, b0);
  not not_10 (not_10_out, b1);
  not not_11 (not_11_out, b0);
  not not_12 (not_12_out, b2);
  not not_13 (not_13_out, b0);
  not not_14 (not_14_out, b3);
  not not_15 (not_15_out, b0);
  not not_16 (not_16_out, b4);
  not not_17 (not_17_out, b0);
  not not_18 (not_18_out, b5);
  not not_19 (not_19_out, b0);
  not not_20 (not_20_out, b2);
  not not_21 (not_21_out, b0);
  not not_22 (not_22_out, b3);
  not not_23 (not_23_out, b0);
  not not_24 (not_24_out, b4);
  not not_25 (not_25_out, b0);
  not not_26 (not_26_out, b5);
  not not_27 (not_27_out, b0);
  not not_28 (not_28_out, b3);
  not not_29 (not_29_out, b1);
  not not_30 (not_30_out, b2);
  not not_31 (not_31_out, b3);
  not not_32 (not_32_out, b0);
  not not_33 (not_33_out, b4);
  not not_34 (not_34_out, b0);
  not not_35 (not_35_out, b5);
  not not_36 (not_36_out, b1);
  not not_37 (not_37_out, b2);
  not not_38 (not_38_out, b4);
  not not_39 (not_39_out, b5);
  not not_40 (not_40_out, b0);
  not not_41 (not_41_out, b4);
  not not_42 (not_42_out, b1);
  not not_43 (not_43_out, b2);
  not not_44 (not_44_out, b3);
  not not_45 (not_45_out, b4);
  not not_46 (not_46_out, b0);
  not not_47 (not_47_out, b5);
  not not_48 (not_48_out, b1);
  not not_49 (not_49_out, b2);
  not not_50 (not_50_out, b3);
  not not_51 (not_51_out, b5);
  not not_52 (not_52_out, b0);
  not not_53 (not_53_out, b5);
  not not_54 (not_54_out, b1);
  not not_55 (not_55_out, b2);
  not not_56 (not_56_out, b3);
  not not_57 (not_57_out, b5);
  not not_58 (not_58_out, b1);
  not not_59 (not_59_out, b2);
  not not_60 (not_60_out, b4);
  not not_61 (not_61_out, b5);
  not not_62 (not_62_out, b1);
  not not_63 (not_63_out, b2);
  not not_64 (not_64_out, b4);
  and and_1 (and_1_out, b0, b3, b4);
  and and_2 (and_2_out, b0, b2);
  and and_3 (and_3_out, b0, b1);
  and and_4 (and_4_out, not_1_out, b1, b2, b3, b4, b5);
  and and_5 (and_5_out, b0, not_2_out, not_3_out, not_4_out);
  and and_6 (and_6_out, b0, not_5_out, not_6_out, not_7_out, not_8_out);
  and and_7 (and_7_out, not_9_out, not_10_out, b2, b3, b4, b5);
  and and_8 (and_8_out, not_11_out, b1, not_12_out);
  and and_9 (and_9_out, not_13_out, b1, not_14_out);
  and and_10 (and_10_out, not_15_out, b1, not_16_out);
  and and_11 (and_11_out, not_17_out, b1, not_18_out);
  and and_12 (and_12_out, not_19_out, not_20_out, b3, b4, b5);
  and and_13 (and_13_out, not_21_out, b2, not_22_out);
  and and_14 (and_14_out, not_23_out, b2, not_24_out);
  and and_15 (and_15_out, not_25_out, b2, not_26_out);
  and and_16 (and_16_out, not_27_out, not_28_out, b4, b5);
  and and_17 (and_17_out, not_29_out, not_30_out, not_31_out, b4, b5);
  and and_18 (and_18_out, not_32_out, b3, not_33_out);
  and and_19 (and_19_out, not_34_out, b3, not_35_out);
  and and_20 (and_20_out, not_36_out, not_37_out, b3, not_38_out, not_39_out);
  and and_21 (and_21_out, not_40_out, not_41_out, b5);
  and and_22 (and_22_out, not_42_out, not_43_out, not_44_out, not_45_out, b5);
  and and_23 (and_23_out, not_46_out, b4, not_47_out);
  and and_24 (and_24_out, not_48_out, not_49_out, not_50_out, b4, not_51_out);
  and and_25 (and_25_out, not_52_out, not_53_out);
  and and_26 (and_26_out, not_54_out, not_55_out, not_56_out, not_57_out);
  and and_27 (and_27_out, not_58_out, not_59_out, not_60_out, not_61_out);
  and and_28 (ZF, b0, not_62_out, not_63_out, b3, not_64_out, b5);
  or or_1 (BAF, and_1_out, and_2_out, and_3_out);
  or or_2 (s0, and_4_out, and_5_out, and_6_out);
  or or_3 (s1, and_7_out, and_8_out, and_9_out, and_10_out, and_11_out);
  or or_4 (s2, and_12_out, and_13_out, and_14_out, and_15_out);
  or or_5 (s3, and_16_out, and_17_out, and_18_out, and_19_out, and_20_out);
  or or_6 (s4, and_21_out, and_22_out, and_23_out, and_24_out);
  or or_7 (s5, and_25_out, and_26_out, and_27_out);

  assign INV_OP = 1'b1;
endmodule

module DEC (
  input  b0,
  input  b1,
  input  b2,
  input  b3,
  input  b4,
  input  b5,
  output s0,
  output s1,
  output s2,
  output s3,
  output s4,
  output s5,
  output ZF,
  output BAF,
  output INV_OP
);

  wire and_1_out, and_2_out, and_3_out, and_4_out, and_5_out, and_6_out, and_7_out, and_8_out, and_9_out,
       and_10_out, and_11_out, and_12_out, and_13_out, and_14_out, and_15_out, and_16_out, and_17_out,
       and_18_out, and_19_out, and_20_out, and_21_out, and_22_out, and_23_out, and_24_out, and_25_out,
       and_26_out, and_27_out, and_28_out, and_29_out, and_30_out, and_31_out, not_1_out, not_2_out,
       not_3_out, not_4_out, not_5_out, not_6_out, not_7_out, not_8_out, not_9_out, not_10_out, not_11_out,
       not_12_out, not_13_out, not_14_out, not_15_out, not_16_out, not_17_out, not_18_out, not_19_out,
       not_20_out, not_21_out, not_22_out, not_23_out, not_24_out, not_25_out, not_26_out, not_27_out,
       not_28_out, not_29_out, not_30_out, not_31_out, not_32_out, not_33_out, not_34_out, not_35_out,
       not_36_out, not_37_out, not_38_out, not_39_out, not_40_out, not_41_out, not_42_out, not_43_out,
       not_44_out, not_45_out, not_46_out, not_47_out, not_48_out, not_49_out, not_50_out, not_51_out,
       not_52_out, not_53_out, not_54_out, not_55_out, not_56_out, not_57_out, not_58_out, not_59_out,
       not_60_out, not_61_out, not_62_out, not_63_out, not_64_out, not_65_out, not_66_out, not_67_out,
       not_68_out, not_69_out, not_70_out, not_71_out, not_72_out, not_73_out, not_74_out, not_75_out,
       not_76_out, not_77_out, not_78_out, not_79_out, not_80_out, not_81_out, not_82_out, not_83_out;

  not not_1 (not_1_out, b0);
  not not_2 (not_2_out, b1);
  not not_3 (not_3_out, b2);
  not not_4 (not_4_out, b3);
  not not_5 (not_5_out, b4);
  not not_6 (not_6_out, b5);
  not not_7 (not_7_out, b1);
  not not_8 (not_8_out, b2);
  not not_9 (not_9_out, b3);
  not not_10 (not_10_out, b1);
  not not_11 (not_11_out, b2);
  not not_12 (not_12_out, b3);
  not not_13 (not_13_out, b1);
  not not_14 (not_14_out, b2);
  not not_15 (not_15_out, b4);
  not not_16 (not_16_out, b0);
  not not_17 (not_17_out, b0);
  not not_18 (not_18_out, b0);
  not not_19 (not_19_out, b0);
  not not_20 (not_20_out, b1);
  not not_21 (not_21_out, b2);
  not not_22 (not_22_out, b3);
  not not_23 (not_23_out, b4);
  not not_24 (not_24_out, b5);
  not not_25 (not_25_out, b0);
  not not_26 (not_26_out, b0);
  not not_27 (not_27_out, b0);
  not not_28 (not_28_out, b0);
  not not_29 (not_29_out, b2);
  not not_30 (not_30_out, b3);
  not not_31 (not_31_out, b4);
  not not_32 (not_32_out, b5);
  not not_33 (not_33_out, b1);
  not not_34 (not_34_out, b2);
  not not_35 (not_35_out, b3);
  not not_36 (not_36_out, b4);
  not not_37 (not_37_out, b5);
  not not_38 (not_38_out, b0);
  not not_39 (not_39_out, b3);
  not not_40 (not_40_out, b4);
  not not_41 (not_41_out, b5);
  not not_42 (not_42_out, b1);
  not not_43 (not_43_out, b2);
  not not_44 (not_44_out, b3);
  not not_45 (not_45_out, b4);
  not not_46 (not_46_out, b5);
  not not_47 (not_47_out, b0);
  not not_48 (not_48_out, b1);
  not not_49 (not_49_out, b2);
  not not_50 (not_50_out, b4);
  not not_51 (not_51_out, b0);
  not not_52 (not_52_out, b0);
  not not_53 (not_53_out, b1);
  not not_54 (not_54_out, b2);
  not not_55 (not_55_out, b3);
  not not_56 (not_56_out, b0);
  not not_57 (not_57_out, b4);
  not not_58 (not_58_out, b5);
  not not_59 (not_59_out, b0);
  not not_60 (not_60_out, b4);
  not not_61 (not_61_out, b5);
  not not_62 (not_62_out, b0);
  not not_63 (not_63_out, b4);
  not not_64 (not_64_out, b5);
  not not_65 (not_65_out, b1);
  not not_66 (not_66_out, b2);
  not not_67 (not_67_out, b4);
  not not_68 (not_68_out, b5);
  not not_69 (not_69_out, b0);
  not not_70 (not_70_out, b5);
  not not_71 (not_71_out, b1);
  not not_72 (not_72_out, b2);
  not not_73 (not_73_out, b3);
  not not_74 (not_74_out, b5);
  not not_75 (not_75_out, b1);
  not not_76 (not_76_out, b2);
  not not_77 (not_77_out, b4);
  not not_78 (not_78_out, b5);
  not not_79 (not_79_out, b0);
  not not_80 (not_80_out, b1);
  not not_81 (not_81_out, b2);
  not not_82 (not_82_out, b3);
  not not_83 (not_83_out, b4);
  and and_1 (and_1_out, b0, b3, b4);
  and and_2 (and_2_out, b0, b2);
  and and_3 (and_3_out, b0, b1);
  and and_4 (and_4_out, not_1_out, not_2_out, not_3_out, not_4_out, not_5_out, not_6_out);
  and and_5 (and_5_out, b0, not_7_out, not_8_out, not_9_out, b5);
  and and_6 (and_6_out, b0, not_10_out, not_11_out, not_12_out, b4);
  and and_7 (and_7_out, b0, not_13_out, not_14_out, b3, not_15_out);
  and and_8 (and_8_out, not_16_out, b1, b5);
  and and_9 (and_9_out, not_17_out, b1, b4);
  and and_10 (and_10_out, not_18_out, b1, b3);
  and and_11 (and_11_out, not_19_out, b1, b2);
  and and_12 (and_12_out, b0, not_20_out, not_21_out, not_22_out, not_23_out, not_24_out);
  and and_13 (and_13_out, not_25_out, b2, b5);
  and and_14 (and_14_out, not_26_out, b2, b4);
  and and_15 (and_15_out, not_27_out, b2, b3);
  and and_16 (and_16_out, not_28_out, b1, not_29_out, not_30_out, not_31_out, not_32_out);
  and and_17 (and_17_out, b0, not_33_out, not_34_out, not_35_out, not_36_out, not_37_out);
  and and_18 (and_18_out, not_38_out, not_39_out, not_40_out, not_41_out);
  and and_19 (and_19_out, not_42_out, not_43_out, not_44_out, not_45_out, not_46_out);
  and and_20 (and_20_out, not_47_out, b3, b5);
  and and_21 (and_21_out, not_48_out, not_49_out, b3, not_50_out, b5);
  and and_22 (and_22_out, not_51_out, b3, b4);
  and and_23 (and_23_out, not_52_out, b4, b5);
  and and_24 (and_24_out, not_53_out, not_54_out, not_55_out, b4, b5);
  and and_25 (and_25_out, not_56_out, b3, not_57_out, not_58_out);
  and and_26 (and_26_out, not_59_out, b2, not_60_out, not_61_out);
  and and_27 (and_27_out, not_62_out, b1, not_63_out, not_64_out);
  and and_28 (and_28_out, b0, not_65_out, not_66_out, not_67_out, not_68_out);
  and and_29 (and_29_out, not_69_out, not_70_out);
  and and_30 (and_30_out, not_71_out, not_72_out, not_73_out, not_74_out);
  and and_31 (and_31_out, not_75_out, not_76_out, not_77_out, not_78_out);
  and and_32 (ZF, not_79_out, not_80_out, not_81_out, not_82_out, not_83_out, b5);
  or or_1 (BAF, and_1_out, and_2_out, and_3_out);
  or or_2 (s0, and_4_out, and_5_out, and_6_out, and_7_out);
  or or_3 (s1, and_8_out, and_9_out, and_10_out, and_11_out, and_12_out);
  or or_4 (s2, and_13_out, and_14_out, and_15_out, and_16_out, and_17_out);
  or or_5 (s3, and_18_out, and_19_out, and_20_out, and_21_out, and_22_out);
  or or_6 (s4, and_23_out, and_24_out, and_25_out, and_26_out, and_27_out, and_28_out);
  or or_7 (s5, and_29_out, and_30_out, and_31_out);

  assign INV_OP = 1'b1;
endmodule

module CMPZ (
  input  b0,
  input  b1,
  input  b2,
  input  b3,
  input  b4,
  input  b5,
  output s0,
  output s1,
  output s2,
  output s3,
  output s4,
  output s5,
  output ZF,
  output INV_OP,
  output BAF
);

  wire not_1_out, not_2_out, not_3_out, not_4_out, not_5_out, not_6_out;

  not not_1 (not_1_out, b0);
  not not_2 (not_2_out, b1);
  not not_3 (not_3_out, b2);
  not not_4 (not_4_out, b3);
  not not_5 (not_5_out, b4);
  not not_6 (not_6_out, b5);
  and and_1 (ZF, not_1_out, not_2_out, not_3_out, not_4_out, not_5_out, not_6_out);

  assign BAF = 1'b0;
  assign INV_OP = 1'b1;
  assign s0 = 1'b0;
  assign s1 = 1'b0;
  assign s2 = 1'b0;
  assign s3 = 1'b0;
  assign s4 = 1'b0;
  assign s5 = 1'b0;
endmodule

module INV (
  input  b0,
  input  b1,
  input  b2,
  input  b3,
  input  b4,
  input  b5,
  output x0,
  output x1,
  output x2,
  output x3,
  output x4,
  output x5,
  output ZF,
  output BAF,
  output INV_OP
);

  wire and_1_out, and_2_out, and_3_out, and_4_out, and_5_out, and_6_out, and_7_out, and_8_out, and_9_out,
       and_10_out, and_11_out, and_12_out, and_13_out, and_14_out, and_15_out, and_16_out, and_17_out,
       and_18_out, and_19_out, and_20_out, and_21_out, and_22_out, and_23_out, and_24_out, and_25_out,
       and_26_out, and_27_out, and_28_out, and_29_out, and_31_out, and_32_out, and_33_out, and_34_out,
       and_35_out, and_36_out, and_37_out, and_38_out, and_39_out, not_1_out, not_2_out, not_3_out,
       not_4_out, not_5_out, not_6_out, not_7_out, not_8_out, not_9_out, not_10_out, not_11_out, not_12_out,
       not_13_out, not_14_out, not_15_out, not_16_out, not_17_out, not_18_out, not_19_out, not_20_out,
       not_21_out, not_22_out, not_23_out, not_24_out, not_25_out, not_26_out, not_27_out, not_28_out,
       not_29_out, not_30_out, not_31_out, not_32_out, not_33_out, not_34_out, not_35_out, not_36_out,
       not_37_out, not_38_out, not_39_out, not_40_out, not_41_out, not_42_out, not_43_out, not_44_out,
       not_45_out, not_46_out, not_47_out, not_48_out, not_49_out, not_50_out, not_51_out, not_52_out,
       not_53_out, not_54_out, not_55_out, not_56_out, not_57_out, not_58_out, not_59_out, not_60_out,
       not_61_out, not_62_out, not_63_out, not_64_out, not_65_out, not_66_out, not_67_out, not_68_out,
       not_69_out, not_70_out, not_71_out, not_72_out, not_73_out, not_74_out, not_75_out, not_76_out,
       not_77_out, not_78_out, not_79_out, not_80_out, not_81_out, not_82_out, not_83_out, not_84_out;

  not not_1 (not_1_out, b0);
  not not_2 (not_2_out, b1);
  not not_3 (not_3_out, b0);
  not not_4 (not_4_out, b3);
  not not_5 (not_5_out, b4);
  not not_6 (not_6_out, b1);
  not not_7 (not_7_out, b2);
  not not_8 (not_8_out, b4);
  not not_9 (not_9_out, b0);
  not not_10 (not_10_out, b2);
  not not_11 (not_11_out, b4);
  not not_12 (not_12_out, b0);
  not not_13 (not_13_out, b1);
  not not_14 (not_14_out, b3);
  not not_15 (not_15_out, b4);
  not not_16 (not_16_out, b0);
  not not_17 (not_17_out, b4);
  not not_18 (not_18_out, b0);
  not not_19 (not_19_out, b1);
  not not_20 (not_20_out, b2);
  not not_21 (not_21_out, b3);
  not not_22 (not_22_out, b0);
  not not_23 (not_23_out, b1);
  not not_24 (not_24_out, b2);
  not not_25 (not_25_out, b0);
  not not_26 (not_26_out, b2);
  not not_27 (not_27_out, b4);
  not not_28 (not_28_out, b0);
  not not_29 (not_29_out, b1);
  not not_30 (not_30_out, b2);
  not not_31 (not_31_out, b3);
  not not_32 (not_32_out, b0);
  not not_33 (not_33_out, b1);
  not not_34 (not_34_out, b3);
  not not_35 (not_35_out, b0);
  not not_36 (not_36_out, b2);
  not not_37 (not_37_out, b4);
  not not_38 (not_38_out, b0);
  not not_39 (not_39_out, b3);
  not not_40 (not_40_out, b0);
  not not_41 (not_41_out, b2);
  not not_42 (not_42_out, b0);
  not not_43 (not_43_out, b4);
  not not_44 (not_44_out, b1);
  not not_45 (not_45_out, b2);
  not not_46 (not_46_out, b4);
  not not_47 (not_47_out, b0);
  not not_48 (not_48_out, b1);
  not not_49 (not_49_out, b2);
  not not_50 (not_50_out, b0);
  not not_51 (not_51_out, b1);
  not not_52 (not_52_out, b4);
  not not_53 (not_53_out, b0);
  not not_54 (not_54_out, b3);
  not not_55 (not_55_out, b0);
  not not_56 (not_56_out, b3);
  not not_57 (not_57_out, b0);
  not not_58 (not_58_out, b1);
  not not_59 (not_59_out, b2);
  not not_60 (not_60_out, b3);
  not not_61 (not_61_out, b4);
  not not_62 (not_62_out, b0);
  not not_63 (not_63_out, b4);
  not not_64 (not_64_out, b1);
  not not_65 (not_65_out, b2);
  not not_66 (not_66_out, b3);
  not not_67 (not_67_out, b1);
  not not_68 (not_68_out, b2);
  not not_69 (not_69_out, b4);
  not not_70 (not_70_out, b0);
  not not_71 (not_71_out, b0);
  not not_72 (not_72_out, b0);
  not not_73 (not_73_out, b1);
  not not_74 (not_74_out, b2);
  not not_75 (not_75_out, b3);
  not not_76 (not_76_out, b4);
  not not_77 (not_77_out, b5);
  not not_78 (not_78_out, b5);
  not not_79 (not_79_out, b5);
  not not_80 (not_80_out, b5);
  not not_81 (not_81_out, b5);
  not not_82 (not_82_out, b2);
  not not_83 (not_83_out, b3);
  not not_84 (not_84_out, b5);
  and and_1 (and_1_out, not_1_out, not_2_out, b2, b3, b4, b5);
  and and_2 (and_2_out, not_3_out, b1, b2, not_4_out, not_5_out, b5);
  and and_3 (and_3_out, b0, not_6_out, not_7_out, b3, not_8_out, b5);
  and and_4 (and_4_out, not_9_out, not_10_out, b3, not_11_out, b5);
  and and_5 (and_5_out, not_12_out, not_13_out, b2, not_14_out, not_15_out, b5);
  and and_6 (and_6_out, not_16_out, b1, b3, not_17_out, b5);
  and and_7 (and_7_out, not_18_out, b1, b2, b4, b5);
  and and_8 (and_8_out, b0, not_19_out, not_20_out, not_21_out, b4, b5);
  and and_9 (and_9_out, not_22_out, not_23_out, not_24_out, b4, b5);
  and and_10 (and_10_out, not_25_out, b1, not_26_out, not_27_out, b5);
  and and_11 (and_11_out, not_28_out, b1, b2, b4, b5);
  and and_12 (and_12_out, b0, not_29_out, not_30_out, not_31_out, b5);
  and and_13 (and_13_out, not_32_out, not_33_out, not_34_out, b4, b5);
  and and_14 (and_14_out, not_35_out, not_36_out, b3, not_37_out, b5);
  and and_15 (and_15_out, not_38_out, b2, not_39_out, b4, b5);
  and and_16 (and_16_out, not_40_out, b1, not_41_out, b3, b5);
  and and_17 (and_17_out, not_42_out, b1, b3, not_43_out, b5);
  and and_18 (and_18_out, b0, not_44_out, not_45_out, not_46_out, b5);
  and and_19 (and_19_out, not_47_out, not_48_out, not_49_out, b3, b5);
  and and_20 (and_20_out, not_50_out, not_51_out, b3, not_52_out, b5);
  and and_21 (and_21_out, not_53_out, b2, not_54_out, b4, b5);
  and and_22 (and_22_out, not_55_out, b1, b2, not_56_out, b5);
  and and_23 (and_23_out, not_57_out, b1, b2, b4, b5);
  and and_24 (and_24_out, b0, not_58_out, not_59_out, not_60_out, not_61_out, b5);
  and and_25 (and_25_out, not_62_out, not_63_out, b5);
  and and_26 (and_26_out, not_64_out, not_65_out, not_66_out, b5);
  and and_27 (and_27_out, not_67_out, not_68_out, not_69_out, b5);
  and and_28 (and_28_out, not_70_out, b3, b5);
  and and_29 (and_29_out, not_71_out, b2, b5);
  and and_30 (ZF, not_72_out, not_73_out, not_74_out, not_75_out, not_76_out, not_77_out);
  and and_31 (and_31_out, b4, not_78_out);
  and and_32 (and_32_out, b3, not_79_out);
  and and_33 (and_33_out, b2, not_80_out);
  and and_34 (and_34_out, b1, not_81_out);
  and and_35 (and_35_out, b1, not_82_out, not_83_out, b4);
  and and_36 (and_36_out, b0, not_84_out);
  and and_37 (and_37_out, b0, b3, b4);
  and and_38 (and_38_out, b0, b2);
  and and_39 (and_39_out, b0, b1);
  or or_1 (x0, and_1_out, and_2_out, and_3_out);
  or or_2 (x1, and_4_out, and_5_out, and_6_out, and_7_out, and_8_out);
  or or_3 (x2, and_9_out, and_10_out, and_11_out, and_12_out);
  or or_4 (x3, and_13_out, and_14_out, and_15_out, and_16_out, and_17_out, and_18_out);
  or or_5 (x4, and_19_out, and_20_out, and_21_out, and_22_out, and_23_out, and_24_out);
  or or_6 (x5, and_25_out, and_26_out, and_27_out, and_28_out, and_29_out);
  or or_7 (BAF, and_31_out, and_32_out, and_33_out, and_34_out, and_35_out, and_36_out, and_37_out, and_38_out, and_39_out);

  assign INV_OP = 1'b1;
endmodule

module SUB (
  input  x0,
  input  x1,
  input  x2,
  input  x3,
  input  x4,
  input  x5,
  input  b0,
  input  b1,
  input  b2,
  input  b3,
  input  b4,
  input  b5,
  output [6:0] out_13,
  output s0,
  output s1,
  output s2,
  output s3,
  output s4,
  output s5,
  output ZF,
  output [6:0] out_21,
  output BAF,
  output INV_OP
);

  wire not_1_out, not_2_out, not_3_out, not_4_out, not_5_out, not_6_out, not_7_out, not_8_out, VLD_2_s5,
       VLD_s5;
  wire [5:0] adder_1_out;
  wire [6:6] adder_1_cout;

  VLD VLD (
    .b0(x0), .b1(x1), .b2(x2), .b3(x3), .b4(x4), .b5(x5), .s5(VLD_s5));  // open: s0, s1, s2, s3, s4, ZF, BAF, INV_OP
  VLD VLD_2 (
    .b0(b0), .b1(b1), .b2(b2), .b3(b3), .b4(b4), .b5(b5), .s5(VLD_2_s5));  // open: s0, s1, s2, s3, s4, ZF, BAF, INV_OP
  not not_1 (not_1_out, VLD_s5);
  not not_2 (not_2_out, VLD_2_s5);
  Adder #(.width(6)) adder_1 (
    .a(6'b100110), .b({x0, x1, x2, x3, x4, x5}), .out(adder_1_out), .cout(adder_1_cout[6]));  // open: cin
  or or_1 (BAF, not_1_out, not_2_out);
  Divider #(.width(7)) divider_1 (.a(out_13), .b(7'b0100110), .rem(out_21));  // open: out, upper
  Subtractor #(.width(7)) subtractor_1 (
    .a({adder_1_cout[6], adder_1_out}), .b({1'b0, b0, b1, b2, b3, b4, b5}), .out(out_13));  // open: bin, bout
  not not_3 (not_3_out, out_21[5]);
  not not_4 (not_4_out, out_21[4]);
  not not_5 (not_5_out, out_21[3]);
  not not_6 (not_6_out, out_21[2]);
  not not_7 (not_7_out, out_21[1]);
  not not_8 (not_8_out, out_21[0]);
  and and_1 (ZF, not_3_out, not_4_out, not_5_out, not_6_out, not_7_out, not_8_out);

  assign INV_OP = 1'b1;
  assign s0 = out_21[5];
  assign s1 = out_21[4];
  assign s2 = out_21[3];
  assign s3 = out_21[2];
  assign s4 = out_21[1];
  assign s5 = out_21[0];
endmodule

module MUL (
  input  x0,
  input  x1,
  input  x2,
  input  x3,
  input  x4,
  input  x5,
  input  b0,
  input  b1,
  input  b2,
  input  b3,
  input  b4,
  input  b5,
  output z0,
  output z1,
  output z2,
  output z3,
  output z4,
  output z5,
  output ZF,
  output BAF,
  output INV_OP
);

  wire not_1_out, not_2_out, not_3_out, not_4_out, not_5_out, not_6_out, not_7_out, not_8_out, VLD_2_s5,
       VLD_s5;
  wire [5:0] multiplier_1_cout, multiplier_1_out;
  wire [11:6] divider_1_rem;

  VLD VLD (
    .b0(x0), .b1(x1), .b2(x2), .b3(x3), .b4(x4), .b5(x5), .s5(VLD_s5));  // open: s0, s1, s2, s3, s4, ZF, BAF, INV_OP
  VLD VLD_2 (
    .b0(b0), .b1(b1), .b2(b2), .b3(b3), .b4(b4), .b5(b5), .s5(VLD_2_s5));  // open: s0, s1, s2, s3, s4, ZF, BAF, INV_OP
  not not_1 (not_1_out, VLD_s5);
  not not_2 (not_2_out, VLD_2_s5);
  not not_3 (not_3_out, z5);
  not not_4 (not_4_out, z4);
  not not_5 (not_5_out, z3);
  and and_1 (ZF, not_3_out, not_4_out, not_5_out, not_6_out, not_7_out, not_8_out);
  not not_6 (not_6_out, z2);
  not not_7 (not_7_out, z1);
  not not_8 (not_8_out, z0);
  or or_1 (BAF, not_1_out, not_2_out);
  Multiplier #(.width(6)) multiplier_1 (
    .a({x0, x1, x2, x3, x4, x5}), .b({b0, b1, b2, b3, b4, b5}), .out(multiplier_1_out),
    .cout(multiplier_1_cout));  // open: cin
  Divider #(.width(12)) divider_1 (
    .a({multiplier_1_cout, multiplier_1_out}), .b(12'h26), .rem({divider_1_rem, z0, z1, z2, z3, z4, z5}));  // open: out, upper

  assign INV_OP = 1'b1;
endmodule

module DIV (
  input  x0,
  input  x1,
  input  x2,
  input  x3,
  input  x4,
  input  x5,
  input  b0,
  input  b1,
  input  b2,
  input  b3,
  input  b4,
  input  b5,
  output [11:0] out_13,
  output z0,
  output z1,
  output z2,
  output z3,
  output z4,
  output z5,
  output ZF,
  output BAF,
  output INV_OP
);

  wire inv_1_baf, not_1_out, not_2_out, not_3_out, not_4_out, not_5_out, not_6_out, not_7_out, not_8_out,
       VLD_2_s5, VLD_s5;
  wire [5:0] inv_1_x5;
  wire [11:6] divider_1_rem;

  VLD VLD (
    .b0(x0), .b1(x1), .b2(x2), .b3(x3), .b4(x4), .b5(x5), .s5(VLD_s5));  // open: s0, s1, s2, s3, s4, ZF, BAF, INV_OP
  VLD VLD_2 (
    .b0(b0), .b1(b1), .b2(b2), .b3(b3), .b4(b4), .b5(b5), .s5(VLD_2_s5));  // open: s0, s1, s2, s3, s4, ZF, BAF, INV_OP
  not not_1 (not_1_out, VLD_s5);
  not not_2 (not_2_out, VLD_2_s5);
  not not_3 (not_3_out, z5);
  not not_4 (not_4_out, z4);
  not not_5 (not_5_out, z3);
  and and_1 (ZF, not_3_out, not_4_out, not_5_out, not_6_out, not_7_out, not_8_out);
  not not_6 (not_6_out, z2);
  not not_7 (not_7_out, z1);
  not not_8 (not_8_out, z0);
  or or_1 (BAF, not_1_out, inv_1_baf, not_2_out);
  Multiplier #(.width(6)) multiplier_1 (
    .a({x0, x1, x2, x3, x4, x5}), .b(inv_1_x5), .out(out_13[5:0]), .cout(out_13[11:6]));  // open: cin
  Divider #(.width(12)) divider_1 (
    .a(out_13), .b(12'h26), .rem({divider_1_rem, z0, z1, z2, z3, z4, z5}));  // open: out, upper
  INV inv_1 (
    .b0(b0), .b1(b1), .b2(b2), .b3(b3), .b4(b4), .b5(b5), .x0(inv_1_x5[5]), .x1(inv_1_x5[4]),
    .x2(inv_1_x5[3]), .x3(inv_1_x5[2]), .x4(inv_1_x5[1]), .x5(inv_1_x5[0]), .BAF(inv_1_baf));  // open: ZF, INV_OP

  assign INV_OP = 1'b1;
endmodule

module SHL (
  input  b0,
  input  b1,
  input  b2,
  input  b3,
  input  b4,
  input  b5,
  output s0,
  output s1,
  output s2,
  output s3,
  output s4,
  output s5,
  output ZF,
  output BAF,
  output INV_OP
);

  wire not_1_out, not_2_out, not_3_out, not_4_out, not_5_out;

  not not_1 (not_1_out, b1);
  not not_2 (not_2_out, b2);
  not not_3 (not_3_out, b3);
  not not_4 (not_4_out, b4);
  not not_5 (not_5_out, b5);
  and and_1 (ZF, not_1_out, not_2_out, not_3_out, not_4_out, not_5_out);

  assign BAF = 1'b0;
  assign INV_OP = 1'b1;
  assign s0 = b1;
  assign s1 = b2;
  assign s2 = b3;
  assign s3 = b4;
  assign s4 = b5;
  assign s5 = 1'b0;
endmodule

module SHR (
  input  b0,
  input  b1,
  input  b2,
  input  b3,
  input  b4,
  input  b5,
  output s0,
  output s1,
  output s2,
  output s3,
  output s4,
  output s5,
  output ZF,
  output BAF,
  output INV_OP
);

  wire not_1_out, not_2_out, not_3_out, not_4_out, not_5_out;

  not not_1 (not_1_out, b0);
  not not_2 (not_2_out, b1);
  not not_3 (not_3_out, b2);
  not not_4 (not_4_out, b3);
  not not_5 (not_5_out, b4);
  and and_1 (ZF, not_1_out, not_2_out, not_3_out, not_4_out, not_5_out);

  assign BAF = 1'b0;
  assign INV_OP = 1'b1;
  assign s0 = 1'b0;
  assign s1 = b0;
  assign s2 = b1;
  assign s3 = b2;
  assign s4 = b3;
  assign s5 = b4;
endmodule

module ROL (
  input  b0,
  input  b1,
  input  b2,
  input  b3,
  input  b4,
  input  b5,
  output s0,
  output s1,
  output s2,
  output s3,
  output s4,
  output s5,
  output ZF,
  output BAF,
  output INV_OP
);

  wire not_1_out, not_2_out, not_3_out, not_4_out, not_5_out, not_6_out;

  not not_1 (not_1_out, b0);
  not not_2 (not_2_out, b1);
  not not_3 (not_3_out, b2);
  not not_4 (not_4_out, b3);
  not not_5 (not_5_out, b4);
  not not_6 (not_6_out, b5);
  and and_1 (ZF, not_1_out, not_2_out, not_3_out, not_4_out, not_5_out, not_6_out);

  assign BAF = 1'b0;
  assign INV_OP = 1'b1;
  assign s0 = b1;
  assign s1 = b2;
  assign s2 = b3;
  assign s3 = b4;
  assign s4 = b5;
  assign s5 = b0;
endmodule

module ROR (
  input  b0,
  input  b1,
  input  b2,
  input  b3,
  input  b4,
  input  b5,
  output s0,
  output s1,
  output s2,
  output s3,
  output s4,
  output s5,
  output ZF,
  output BAF,
  output INV_OP
);

  wire not_1_out, not_2_out, not_3_out, not_4_out, not_5_out, not_6_out;

  not not_1 (not_1_out, b0);
  not not_2 (not_2_out, b1);
  not not_3 (not_3_out, b2);
  not not_4 (not_4_out, b3);
  not not_5 (not_5_out, b4);
  not not_6 (not_6_out, b5);
  and and_1 (ZF, not_1_out, not_2_out, not_3_out, not_4_out, not_5_out, not_6_out);

  assign BAF = 1'b0;
  assign INV_OP = 1'b1;
  assign s0 = b5;
  assign s1 = b0;
  assign s2 = b1;
  assign s3 = b2;
  assign s4 = b3;
  assign s5 = b4;
endmodule

module XOR (
  input  b0,
  input  b1,
  input  b2,
  input  b3,
  input  b4,
  input  b5,
  input  x0,
  input  x1,
  input  x2,
  input  x3,
  input  x4,
  input  x5,
  output BAF,
  output INV_OP,
  output s0,
  output s1,
  output s2,
  output s3,
  output s4,
  output s5,
  output ZF
);

  wire not_1_out, not_2_out, not_3_out, not_4_out, not_5_out, not_6_out, not_7_out, not_8_out, VLD_2_s5,
       VLD_s5;

  VLD VLD (
    .b0(b0), .b1(b1), .b2(b2), .b3(b3), .b4(b4), .b5(b5), .s5(VLD_s5));  // open: s0, s1, s2, s3, s4, ZF, BAF, INV_OP
  not not_1 (not_1_out, VLD_s5);
  not not_2 (not_2_out, VLD_2_s5);
  and and_1 (BAF, not_1_out, not_2_out);
  VLD VLD_2 (
    .b0(x0), .b1(x1), .b2(x2), .b3(x3), .b4(x4), .b5(x5), .s5(VLD_2_s5));  // open: s0, s1, s2, s3, s4, ZF, BAF, INV_OP
  assign {s5, s4, s3, s2, s1, s0} = {b5, b4, b3, b2, b1, b0} ^ {x5, x4, x3, x2, x1, x0};  // XOR_Gate xor_1, 6 bits wide
  not not_3 (not_3_out, s4);
  not not_4 (not_4_out, s3);
  not not_5 (not_5_out, s1);
  not not_6 (not_6_out, s0);
  not not_7 (not_7_out, s2);
  not not_8 (not_8_out, s5);
  and and_2 (ZF, not_8_out, not_3_out, not_4_out, not_7_out, not_5_out, not_6_out);

  assign INV_OP = 1'b1;
endmodule

module AND (
  input  b0,
  input  b1,
  input  b2,
  input  b3,
  input  b4,
  input  b5,
  input  x0,
  input  x1,
  input  x2,
  input  x3,
  input  x4,
  input  x5,
  output BAF,
  output INV_OP,
  output s0,
  output s1,
  output s2,
  output s3,
  output s4,
  output s5,
  output ZF
);

  wire not_1_out, not_2_out, not_3_out, not_4_out, not_5_out, not_6_out, not_7_out, not_8_out, VLD_2_s5,
       VLD_s5;

  VLD VLD (
    .b0(b0), .b1(b1), .b2(b2), .b3(b3), .b4(b4), .b5(b5), .s5(VLD_s5));  // open: s0, s1, s2, s3, s4, ZF, BAF, INV_OP
  not not_1 (not_1_out, VLD_2_s5);
  not not_2 (not_2_out, VLD_s5);
  and and_1 (BAF, not_2_out, not_1_out);
  VLD VLD_2 (
    .b0(x0), .b1(x1), .b2(x2), .b3(x3), .b4(x4), .b5(x5), .s5(VLD_2_s5));  // open: s0, s1, s2, s3, s4, ZF, BAF, INV_OP
  assign {s5, s4, s3, s2, s1, s0} = {x5, x4, x3, x2, x1, x0} & {b5, b4, b3, b2, b1, b0};  // AND_Gate AND_2, 6 bits wide
  not not_3 (not_3_out, s3);
  not not_4 (not_4_out, s4);
  not not_5 (not_5_out, s2);
  not not_6 (not_6_out, s5);
  and and_3 (ZF, not_6_out, not_4_out, not_3_out, not_5_out, not_8_out, not_7_out);
  not not_7 (not_7_out, s0);
  not not_8 (not_8_out, s1);

  assign INV_OP = 1'b1;
endmodule

module OR (
  input  b0,
  input  b1,
  input  b2,
  input  b3,
  input  b4,
  input  b5,
  input  x0,
  input  x1,
  input  x2,
  input  x3,
  input  x4,
  input  x5,
  output BAF,
  output INV_OP,
  output s0,
  output s1,
  output s2,
  output s3,
  output s4,
  output s5,
  output ZF
);

  wire not_1_out, not_2_out, not_3_out, not_4_out, not_5_out, not_6_out, not_7_out, not_8_out, VLD_2_s5,
       VLD_s5;

  VLD VLD (
    .b0(b0), .b1(b1), .b2(b2), .b3(b3), .b4(b4), .b5(b5), .s5(VLD_s5));  // open: s0, s1, s2, s3, s4, ZF, BAF, INV_OP
  not not_1 (not_1_out, VLD_s5);
  not not_2 (not_2_out, VLD_2_s5);
  and and_1 (BAF, not_1_out, not_2_out);
  VLD VLD_2 (
    .b0(x0), .b1(x1), .b2(x2), .b3(x3), .b4(x4), .b5(x5), .s5(VLD_2_s5));  // open: s0, s1, s2, s3, s4, ZF, BAF, INV_OP
  assign {s5, s4, s3, s2, s1, s0} = {b5, b4, b3, b2, b1, b0} | {x5, x4, x3, x2, x1, x0};  // OR_Gate or_1, 6 bits wide
  not not_3 (not_3_out, s4);
  not not_4 (not_4_out, s5);
  not not_5 (not_5_out, s2);
  not not_6 (not_6_out, s3);
  not not_7 (not_7_out, s1);
  and and_2 (ZF, not_4_out, not_3_out, not_6_out, not_5_out, not_7_out, not_8_out);
  not not_8 (not_8_out, s0);

  assign INV_OP = 1'b1;
endmodule

module NOT (
  input  b0,
  input  b1,
  input  b2,
  input  b3,
  input  b4,
  input  b5,
  output s0,
  output s1,
  output s2,
  output s3,
  output s4,
  output s5,
  output ZF,
  output BAF,
  output INV_OP
);

  not not_1 (s0, b0);
  not not_2 (s1, b1);
  not not_3 (s2, b2);
  not not_4 (s3, b3);
  not not_5 (s4, b4);
  not not_6 (s5, b5);
  and and_1 (ZF, b0, b1, b2, b3, b4, b5);

  assign BAF = 1'b0;
  assign INV_OP = 1'b1;
endmodule

module N1 (
  input  b0,
  input  b1,
  input  b2,
  input  b3,
  input  b4,
  input  b5,
  output s0,
  output s1,
  output s2,
  output s3,
  output s4,
  output s5,
  output ZF,
  output BAF,
  output INV_OP
);

  wire and_1_out, and_2_out, and_3_out, and_4_out, and_5_out, and_6_out, and_7_out, and_8_out, and_9_out,
       and_10_out, and_11_out, and_12_out, and_13_out, and_14_out, and_15_out, and_16_out, and_17_out,
       and_18_out, and_19_out, and_20_out, and_21_out, and_22_out, and_23_out, and_24_out, and_25_out,
       and_26_out, and_27_out, and_28_out, and_29_out, and_30_out, and_31_out, and_32_out, and_33_out,
       and_34_out, and_35_out, and_36_out, and_37_out, and_38_out, and_39_out, and_40_out, and_41_out,
       and_42_out, and_43_out, and_44_out, and_45_out, and_46_out, and_47_out, and_48_out, and_49_out,
       and_50_out, and_51_out, and_52_out, and_53_out, and_54_out, and_55_out, and_56_out, and_57_out,
       and_58_out, and_59_out, and_60_out, and_61_out, and_62_out, and_63_out, and_64_out, and_65_out,
       and_66_out, and_67_out, and_68_out, and_69_out, and_70_out, and_71_out, and_72_out, and_73_out,
       not_1_out, not_2_out, not_3_out, not_4_out, not_5_out, not_6_out, not_7_out, not_8_out, not_9_out,
       not_10_out, not_11_out, not_12_out, not_13_out, not_14_out, not_15_out, not_16_out, not_17_out,
       not_18_out, not_19_out, not_20_out, not_21_out, not_22_out, not_23_out, not_24_out, not_25_out,
       not_26_out, not_27_out, not_28_out, not_29_out, not_30_out, not_31_out, not_32_out, not_33_out,
       not_34_out, not_35_out, not_36_out, not_37_out, not_38_out, not_39_out, not_40_out, not_41_out,
       not_42_out, not_43_out, not_44_out, not_45_out, not_46_out, not_47_out, not_48_out, not_49_out,
       not_50_out, not_51_out, not_52_out, not_53_out, not_54_out, not_55_out, not_56_out, not_57_out,
       not_58_out, not_59_out, not_60_out, not_61_out, not_62_out, not_63_out, not_64_out, not_65_out,
       not_66_out, not_67_out, not_68_out, not_69_out, not_70_out, not_71_out, not_72_out, not_73_out,
       not_74_out, not_75_out, not_76_out, not_77_out, not_78_out, not_79_out, not_80_out, not_81_out,
       not_82_out, not_83_out, not_84_out, not_85_out, not_86_out, not_87_out, not_88_out, not_89_out,
       not_90_out, not_91_out, not_92_out, not_93_out, not_94_out, not_95_out, not_96_out, not_97_out,
       not_98_out, not_99_out, not_100_out, not_101_out, not_102_out, not_103_out, not_104_out, not_105_out,
       not_106_out, not_107_out, not_108_out, not_109_out, not_110_out, not_111_out, not_112_out,
       not_113_out, not_114_out, not_115_out, not_116_out, not_117_out, not_118_out, not_119_out,
       not_120_out, not_121_out, not_122_out, not_123_out, not_124_out, not_125_out, not_126_out,
       not_127_out, not_128_out, not_129_out, not_130_out, not_131_out, not_132_out, not_133_out,
       not_134_out, not_135_out, not_136_out, not_137_out, not_138_out, not_139_out, not_140_out,
       not_141_out, not_142_out, not_143_out, not_144_out, not_145_out, not_146_out, not_147_out,
       not_148_out, not_149_out, not_150_out, not_151_out, not_152_out, not_153_out, not_154_out,
       not_155_out, not_156_out, not_157_out, not_158_out, not_159_out, not_160_out, not_161_out,
       not_162_out, not_163_out, not_164_out, not_165_out, not_166_out, not_167_out, not_168_out,
       not_169_out, not_170_out, not_171_out, not_172_out, not_173_out, not_174_out, not_175_out,
       not_176_out, not_177_out;

  and and_1 (and_1_out, b2, b3, b4, b5);
  and and_2 (and_2_out, b1, b3, b4, b5);
  and and_3 (and_3_out, b1, b2, b4, b5);
  and and_4 (and_4_out, b1, b2, b3, b5);
  and and_5 (and_5_out, b1, b2, b3, b4);
  and and_6 (and_6_out, b0, b3, b4, b5);
  and and_7 (and_7_out, b0, b2, b4, b5);
  and and_8 (and_8_out, b0, b2, b3, b5);
  and and_9 (and_9_out, b0, b2, b3, b4);
  and and_10 (and_10_out, b0, b1, b4, b5);
  and and_11 (and_11_out, b0, b1, b3, b5);
  and and_12 (and_12_out, b0, b1, b3, b4);
  and and_13 (and_13_out, b0, b1, b2, b5);
  and and_14 (and_14_out, b0, b1, b2, b4);
  and and_15 (and_15_out, b0, b1, b2, b3);
  not not_1 (not_1_out, b0);
  not not_2 (not_2_out, b1);
  not not_3 (not_3_out, b2);
  not not_4 (not_4_out, b0);
  not not_5 (not_5_out, b1);
  not not_6 (not_6_out, b2);
  not not_7 (not_7_out, b0);
  not not_8 (not_8_out, b1);
  not not_9 (not_9_out, b2);
  not not_10 (not_10_out, b0);
  not not_11 (not_11_out, b1);
  not not_12 (not_12_out, b3);
  not not_13 (not_13_out, b0);
  not not_14 (not_14_out, b1);
  not not_15 (not_15_out, b3);
  not not_16 (not_16_out, b0);
  not not_17 (not_17_out, b1);
  not not_18 (not_18_out, b4);
  not not_19 (not_19_out, b0);
  not not_20 (not_20_out, b1);
  not not_21 (not_21_out, b5);
  not not_22 (not_22_out, b0);
  not not_23 (not_23_out, b2);
  not not_24 (not_24_out, b3);
  not not_25 (not_25_out, b0);
  not not_26 (not_26_out, b2);
  not not_27 (not_27_out, b3);
  not not_28 (not_28_out, b0);
  not not_29 (not_29_out, b2);
  not not_30 (not_30_out, b4);
  not not_31 (not_31_out, b0);
  not not_32 (not_32_out, b2);
  not not_33 (not_33_out, b5);
  not not_34 (not_34_out, b0);
  not not_35 (not_35_out, b3);
  not not_36 (not_36_out, b4);
  not not_37 (not_37_out, b0);
  not not_38 (not_38_out, b3);
  not not_39 (not_39_out, b5);
  not not_40 (not_40_out, b0);
  not not_41 (not_41_out, b4);
  not not_42 (not_42_out, b5);
  not not_43 (not_43_out, b1);
  not not_44 (not_44_out, b2);
  not not_45 (not_45_out, b3);
  not not_46 (not_46_out, b1);
  not not_47 (not_47_out, b2);
  not not_48 (not_48_out, b3);
  not not_49 (not_49_out, b1);
  not not_50 (not_50_out, b2);
  not not_51 (not_51_out, b4);
  not not_52 (not_52_out, b1);
  not not_53 (not_53_out, b2);
  not not_54 (not_54_out, b5);
  not not_55 (not_55_out, b1);
  not not_56 (not_56_out, b3);
  not not_57 (not_57_out, b4);
  not not_58 (not_58_out, b1);
  not not_59 (not_59_out, b3);
  not not_60 (not_60_out, b5);
  not not_61 (not_61_out, b1);
  not not_62 (not_62_out, b4);
  not not_63 (not_63_out, b5);
  not not_64 (not_64_out, b2);
  not not_65 (not_65_out, b3);
  not not_66 (not_66_out, b4);
  not not_67 (not_67_out, b2);
  not not_68 (not_68_out, b3);
  not not_69 (not_69_out, b5);
  not not_70 (not_70_out, b2);
  not not_71 (not_71_out, b4);
  not not_72 (not_72_out, b5);
  not not_73 (not_73_out, b3);
  not not_74 (not_74_out, b4);
  not not_75 (not_75_out, b5);
  not not_76 (not_76_out, b0);
  not not_77 (not_77_out, b1);
  not not_78 (not_78_out, b2);
  not not_79 (not_79_out, b3);
  not not_80 (not_80_out, b4);
  not not_81 (not_81_out, b0);
  not not_82 (not_82_out, b1);
  not not_83 (not_83_out, b2);
  not not_84 (not_84_out, b3);
  not not_85 (not_85_out, b5);
  not not_86 (not_86_out, b0);
  not not_87 (not_87_out, b1);
  not not_88 (not_88_out, b2);
  not not_89 (not_89_out, b4);
  not not_90 (not_90_out, b5);
  not not_91 (not_91_out, b0);
  not not_92 (not_92_out, b1);
  not not_93 (not_93_out, b2);
  not not_94 (not_94_out, b0);
  not not_95 (not_95_out, b1);
  not not_96 (not_96_out, b3);
  not not_97 (not_97_out, b4);
  not not_98 (not_98_out, b5);
  not not_99 (not_99_out, b0);
  not not_100 (not_100_out, b1);
  not not_101 (not_101_out, b3);
  not not_102 (not_102_out, b0);
  not not_103 (not_103_out, b1);
  not not_104 (not_104_out, b4);
  not not_105 (not_105_out, b0);
  not not_106 (not_106_out, b1);
  not not_107 (not_107_out, b5);
  not not_108 (not_108_out, b0);
  not not_109 (not_109_out, b2);
  not not_110 (not_110_out, b3);
  not not_111 (not_111_out, b4);
  not not_112 (not_112_out, b5);
  not not_113 (not_113_out, b0);
  not not_114 (not_114_out, b2);
  not not_115 (not_115_out, b3);
  not not_116 (not_116_out, b0);
  not not_117 (not_117_out, b2);
  not not_118 (not_118_out, b4);
  not not_119 (not_119_out, b0);
  not not_120 (not_120_out, b2);
  not not_121 (not_121_out, b5);
  not not_122 (not_122_out, b0);
  not not_123 (not_123_out, b3);
  not not_124 (not_124_out, b4);
  not not_125 (not_125_out, b0);
  not not_126 (not_126_out, b3);
  not not_127 (not_127_out, b5);
  not not_128 (not_128_out, b0);
  not not_129 (not_129_out, b4);
  not not_130 (not_130_out, b5);
  not not_131 (not_131_out, b0);
  not not_132 (not_132_out, b1);
  not not_133 (not_133_out, b2);
  not not_134 (not_134_out, b3);
  not not_135 (not_135_out, b4);
  not not_136 (not_136_out, b5);
  not not_137 (not_137_out, b1);
  not not_138 (not_138_out, b2);
  not not_139 (not_139_out, b3);
  not not_140 (not_140_out, b1);
  not not_141 (not_141_out, b2);
  not not_142 (not_142_out, b4);
  not not_143 (not_143_out, b1);
  not not_144 (not_144_out, b2);
  not not_145 (not_145_out, b5);
  not not_146 (not_146_out, b1);
  not not_147 (not_147_out, b3);
  not not_148 (not_148_out, b4);
  not not_149 (not_149_out, b1);
  not not_150 (not_150_out, b3);
  not not_151 (not_151_out, b5);
  not not_152 (not_152_out, b1);
  not not_153 (not_153_out, b4);
  not not_154 (not_154_out, b5);
  not not_155 (not_155_out, b1);
  not not_156 (not_156_out, b2);
  not not_157 (not_157_out, b3);
  not not_158 (not_158_out, b4);
  not not_159 (not_159_out, b2);
  not not_160 (not_160_out, b3);
  not not_161 (not_161_out, b5);
  not not_162 (not_162_out, b2);
  not not_163 (not_163_out, b4);
  not not_164 (not_164_out, b5);
  not not_165 (not_165_out, b2);
  not not_166 (not_166_out, b3);
  not not_167 (not_167_out, b4);
  not not_168 (not_168_out, b5);
  not not_169 (not_169_out, b3);
  not not_170 (not_170_out, b4);
  not not_171 (not_171_out, b5);
  not not_172 (not_172_out, b0);
  not not_173 (not_173_out, b1);
  not not_174 (not_174_out, b2);
  not not_175 (not_175_out, b3);
  not not_176 (not_176_out, b4);
  not not_177 (not_177_out, b5);
  and and_16 (and_16_out, not_1_out, not_2_out, not_3_out, b4, b5);
  and and_17 (and_17_out, not_4_out, not_5_out, not_6_out, b3, b5);
  and and_18 (and_18_out, not_7_out, not_8_out, not_9_out, b3, b4);
  and and_19 (and_19_out, not_10_out, not_11_out, b2, not_12_out, b5);
  and and_20 (and_20_out, not_13_out, not_14_out, b2, not_15_out, b4);
  and and_21 (and_21_out, not_16_out, not_17_out, b2, b3, not_18_out);
  and and_22 (and_22_out, not_19_out, not_20_out, b2, b3, not_21_out);
  and and_23 (and_23_out, not_22_out, b1, not_23_out, not_24_out, b5);
  and and_24 (and_24_out, not_25_out, b1, not_26_out, not_27_out, b4);
  and and_25 (and_25_out, not_28_out, b1, not_29_out, b3, not_30_out);
  and and_26 (and_26_out, not_31_out, b1, not_32_out, b3, not_33_out);
  and and_27 (and_27_out, not_34_out, b1, b2, not_35_out, not_36_out);
  and and_28 (and_28_out, not_37_out, b1, b2, not_38_out, not_39_out);
  and and_29 (and_29_out, not_40_out, b1, b2, not_41_out, not_42_out);
  and and_30 (and_30_out, b0, not_43_out, not_44_out, not_45_out, b5);
  and and_31 (and_31_out, b0, not_46_out, not_47_out, not_48_out, b4);
  and and_32 (and_32_out, b0, not_49_out, not_50_out, b3, not_51_out);
  and and_33 (and_33_out, b0, not_52_out, not_53_out, b3, not_54_out);
  and and_34 (and_34_out, b0, not_55_out, b2, not_56_out, not_57_out);
  and and_35 (and_35_out, b0, not_58_out, b2, not_59_out, not_60_out);
  and and_36 (and_36_out, b0, not_61_out, b2, not_62_out, not_63_out);
  and and_37 (and_37_out, b0, b1, not_64_out, not_65_out, not_66_out);
  and and_38 (and_38_out, b0, b1, not_67_out, not_68_out, not_69_out);
  and and_39 (and_39_out, b0, b1, not_70_out, not_71_out, not_72_out);
  and and_40 (and_40_out, b0, b1, not_73_out, not_74_out, not_75_out);
  and and_41 (and_41_out, b0, b1, b2, b3, b4, b5);
  and and_42 (and_42_out, not_76_out, not_77_out, not_78_out, not_79_out, not_80_out, b5);
  and and_43 (and_43_out, not_81_out, not_82_out, not_83_out, not_84_out, b4, not_85_out);
  and and_44 (and_44_out, not_86_out, not_87_out, not_88_out, b3, not_89_out, not_90_out);
  and and_45 (and_45_out, not_91_out, not_92_out, not_93_out, b3, b4, b5);
  and and_46 (and_46_out, not_94_out, not_95_out, b2, not_96_out, not_97_out, not_98_out);
  and and_47 (and_47_out, not_99_out, not_100_out, b2, not_101_out, b4, b5);
  and and_48 (and_48_out, not_102_out, not_103_out, b2, b3, not_104_out, b5);
  and and_49 (and_49_out, not_105_out, not_106_out, b2, b3, b4, not_107_out);
  and and_50 (and_50_out, not_108_out, b1, not_109_out, not_110_out, not_111_out, not_112_out);
  and and_51 (and_51_out, not_113_out, b1, not_114_out, not_115_out, b4, b5);
  and and_52 (and_52_out, not_116_out, b1, not_117_out, b3, not_118_out, b5);
  and and_53 (and_53_out, not_119_out, b1, not_120_out, b3, b4, not_121_out);
  and and_54 (and_54_out, not_122_out, b1, b2, not_123_out, not_124_out, b5);
  and and_55 (and_55_out, not_125_out, b1, b2, not_126_out, b4, not_127_out);
  and and_56 (and_56_out, not_128_out, b1, b2, b3, not_129_out, not_130_out);
  and and_57 (and_57_out, not_131_out, b1, b2, b3, b4, b5);
  and and_58 (and_58_out, b0, not_132_out, not_133_out, not_134_out, not_135_out, not_136_out);
  and and_59 (and_59_out, b0, not_137_out, not_138_out, not_139_out, b4, b5);
  and and_60 (and_60_out, b0, not_140_out, not_141_out, b3, not_142_out, b5);
  and and_61 (and_61_out, b0, not_143_out, not_144_out, b3, b4, not_145_out);
  and and_62 (and_62_out, b0, not_146_out, b2, not_147_out, not_148_out, b5);
  and and_63 (and_63_out, b0, not_149_out, b2, not_150_out, b4, not_151_out);
  and and_64 (and_64_out, b0, not_152_out, b2, b3, not_153_out, not_154_out);
  and and_65 (and_65_out, b0, not_155_out, b2, b3, b4, b5);
  and and_66 (and_66_out, b0, b1, not_156_out, not_157_out, not_158_out, b5);
  and and_67 (and_67_out, b0, b1, not_159_out, not_160_out, b4, not_161_out);
  and and_68 (and_68_out, b0, b1, not_162_out, b3, not_163_out, not_164_out);
  and and_69 (and_69_out, b0, b1, not_165_out, b3, b4, b5);
  and and_70 (and_70_out, b0, b1, b2, not_166_out, not_167_out, not_168_out);
  and and_71 (and_71_out, b0, b1, b2, not_169_out, b4, b5);
  and and_72 (and_72_out, b0, b1, b2, b3, not_170_out, b5);
  and and_73 (and_73_out, b0, b1, b2, b3, b4, not_171_out);
  and and_74 (ZF, not_172_out, not_173_out, not_174_out, not_175_out, not_176_out, not_177_out);
  or or_1 (s3, and_1_out, and_2_out, and_3_out, and_4_out, and_5_out, and_6_out, and_7_out, and_8_out, and_9_out, and_10_out, and_11_out, and_12_out, and_13_out, and_14_out, and_15_out);
  or or_2 (s4, and_16_out, and_17_out, and_18_out, and_19_out, and_20_out, and_21_out, and_22_out, and_23_out, and_24_out, and_25_out, and_26_out, and_27_out, and_28_out, and_29_out, and_30_out, and_31_out, and_32_out, and_33_out, and_34_out, and_35_out, and_36_out, and_37_out, and_38_out, and_39_out, and_40_out, and_41_out);
  or or_3 (s5, and_42_out, and_43_out, and_44_out, and_45_out, and_46_out, and_47_out, and_48_out, and_49_out, and_50_out, and_51_out, and_52_out, and_53_out, and_54_out, and_55_out, and_56_out, and_57_out, and_58_out, and_59_out, and_60_out, and_61_out, and_62_out, and_63_out, and_64_out, and_65_out, and_66_out, and_67_out, and_68_out, and_69_out, and_70_out, and_71_out, and_72_out, and_73_out);

  assign BAF = 1'b0;
  assign INV_OP = 1'b1;
  assign s0 = 1'b0;
  assign s1 = 1'b0;
  assign s2 = 1'b0;
endmodule

module N0 (
  input  b0,
  input  b1,
  input  b2,
  input  b3,
  input  b4,
  input  b5,
  output s0,
  output s1,
  output s2,
  output s3,
  output s4,
  output s5,
  output ZF,
  output BAF,
  output INV_OP
);

  wire and_2_out, and_3_out, and_4_out, and_5_out, and_6_out, and_7_out, and_8_out, and_9_out, and_10_out,
       and_11_out, and_12_out, and_13_out, and_14_out, and_15_out, and_16_out, and_17_out, and_18_out,
       and_19_out, and_20_out, and_21_out, and_22_out, and_23_out, and_24_out, and_25_out, and_26_out,
       and_27_out, and_28_out, and_29_out, and_30_out, and_31_out, and_32_out, and_33_out, and_34_out,
       and_35_out, and_36_out, and_37_out, and_38_out, and_39_out, and_40_out, and_41_out, and_42_out,
       and_43_out, and_44_out, and_45_out, and_46_out, and_47_out, and_48_out, and_49_out, and_50_out,
       and_51_out, and_52_out, and_53_out, and_54_out, and_55_out, and_56_out, and_57_out, and_58_out,
       and_59_out, and_60_out, and_61_out, and_62_out, and_63_out, and_64_out, and_65_out, and_66_out,
       and_67_out, and_68_out, and_69_out, and_70_out, and_71_out, and_72_out, and_73_out, and_74_out,
       not_1_out, not_2_out, not_3_out, not_4_out, not_5_out, not_6_out, not_7_out, not_8_out, not_9_out,
       not_10_out, not_11_out, not_12_out, not_13_out, not_14_out, not_15_out, not_16_out, not_17_out,
       not_18_out, not_19_out, not_20_out, not_21_out, not_22_out, not_23_out, not_24_out, not_25_out,
       not_26_out, not_27_out, not_28_out, not_29_out, not_30_out, not_31_out, not_32_out, not_33_out,
       not_34_out, not_35_out, not_36_out, not_37_out, not_38_out, not_39_out, not_40_out, not_41_out,
       not_42_out, not_43_out, not_44_out, not_45_out, not_46_out, not_47_out, not_48_out, not_49_out,
       not_50_out, not_51_out, not_52_out, not_53_out, not_54_out, not_55_out, not_56_out, not_57_out,
       not_58_out, not_59_out, not_60_out, not_61_out, not_62_out, not_63_out, not_64_out, not_65_out,
       not_66_out, not_67_out, not_68_out, not_69_out, not_70_out, not_71_out, not_72_out, not_73_out,
       not_74_out, not_75_out, not_76_out, not_77_out, not_78_out, not_79_out, not_80_out, not_81_out,
       not_82_out, not_83_out, not_84_out, not_85_out, not_86_out, not_87_out, not_88_out, not_89_out,
       not_90_out, not_91_out, not_92_out, not_93_out, not_94_out, not_95_out, not_96_out, not_97_out,
       not_98_out, not_99_out, not_100_out, not_101_out, not_102_out, not_103_out, not_104_out, not_105_out,
       not_106_out, not_107_out, not_108_out, not_109_out, not_110_out, not_111_out, not_112_out,
       not_113_out, not_114_out, not_115_out, not_116_out, not_117_out, not_118_out, not_119_out,
       not_120_out, not_121_out, not_122_out, not_123_out, not_124_out, not_125_out, not_126_out,
       not_127_out, not_128_out, not_129_out, not_130_out, not_131_out, not_132_out, not_133_out,
       not_134_out, not_135_out, not_136_out, not_137_out, not_138_out, not_139_out, not_140_out,
       not_141_out, not_142_out, not_143_out, not_144_out, not_145_out, not_146_out, not_147_out,
       not_148_out, not_149_out, not_150_out, not_151_out, not_152_out, not_153_out, not_154_out,
       not_155_out, not_156_out, not_157_out, not_158_out, not_159_out, not_160_out, not_161_out,
       not_162_out, not_163_out, not_164_out, not_165_out, not_166_out, not_167_out, not_168_out,
       not_169_out, not_170_out, not_171_out, not_172_out, not_173_out, not_174_out, not_175_out,
       not_176_out, not_177_out, not_178_out, not_179_out, not_180_out, not_181_out, not_182_out,
       not_183_out, not_184_out, not_185_out, not_186_out, not_187_out, not_188_out, not_189_out,
       not_190_out, not_191_out, not_192_out, not_193_out, not_194_out, not_195_out, not_196_out,
       not_197_out, not_198_out, not_199_out, not_200_out, not_201_out, not_202_out, not_203_out,
       not_204_out, not_205_out, not_206_out, not_207_out, not_208_out, not_209_out, not_210_out,
       not_211_out, not_212_out;

  not not_1 (not_1_out, b0);
  not not_2 (not_2_out, b1);
  not not_3 (not_3_out, b2);
  not not_4 (not_4_out, b3);
  not not_5 (not_5_out, b0);
  not not_6 (not_6_out, b1);
  not not_7 (not_7_out, b2);
  not not_8 (not_8_out, b4);
  not not_9 (not_9_out, b0);
  not not_10 (not_10_out, b1);
  not not_11 (not_11_out, b2);
  not not_12 (not_12_out, b5);
  not not_13 (not_13_out, b0);
  not not_14 (not_14_out, b1);
  not not_15 (not_15_out, b3);
  not not_16 (not_16_out, b4);
  not not_17 (not_17_out, b0);
  not not_18 (not_18_out, b1);
  not not_19 (not_19_out, b3);
  not not_20 (not_20_out, b5);
  not not_21 (not_21_out, b0);
  not not_22 (not_22_out, b1);
  not not_23 (not_23_out, b4);
  not not_24 (not_24_out, b5);
  not not_25 (not_25_out, b0);
  not not_26 (not_26_out, b2);
  not not_27 (not_27_out, b3);
  not not_28 (not_28_out, b4);
  not not_29 (not_29_out, b0);
  not not_30 (not_30_out, b2);
  not not_31 (not_31_out, b3);
  not not_32 (not_32_out, b5);
  not not_33 (not_33_out, b0);
  not not_34 (not_34_out, b2);
  not not_35 (not_35_out, b4);
  not not_36 (not_36_out, b5);
  not not_37 (not_37_out, b0);
  not not_38 (not_38_out, b3);
  not not_39 (not_39_out, b4);
  not not_40 (not_40_out, b5);
  not not_41 (not_41_out, b1);
  not not_42 (not_42_out, b2);
  not not_43 (not_43_out, b3);
  not not_44 (not_44_out, b4);
  not not_45 (not_45_out, b1);
  not not_46 (not_46_out, b2);
  not not_47 (not_47_out, b3);
  not not_48 (not_48_out, b5);
  not not_49 (not_49_out, b1);
  not not_50 (not_50_out, b2);
  not not_51 (not_51_out, b4);
  not not_52 (not_52_out, b5);
  not not_53 (not_53_out, b1);
  not not_54 (not_54_out, b3);
  not not_55 (not_55_out, b4);
  not not_56 (not_56_out, b5);
  not not_57 (not_57_out, b2);
  not not_58 (not_58_out, b3);
  not not_59 (not_59_out, b4);
  not not_60 (not_60_out, b5);
  not not_61 (not_61_out, b0);
  not not_62 (not_62_out, b1);
  not not_63 (not_63_out, b2);
  not not_64 (not_64_out, b3);
  not not_65 (not_65_out, b4);
  not not_66 (not_66_out, b5);
  not not_67 (not_67_out, b0);
  not not_68 (not_68_out, b1);
  not not_69 (not_69_out, b0);
  not not_70 (not_70_out, b1);
  not not_71 (not_71_out, b0);
  not not_72 (not_72_out, b1);
  not not_73 (not_73_out, b0);
  not not_74 (not_74_out, b1);
  not not_75 (not_75_out, b0);
  not not_76 (not_76_out, b2);
  not not_77 (not_77_out, b0);
  not not_78 (not_78_out, b2);
  not not_79 (not_79_out, b0);
  not not_80 (not_80_out, b2);
  not not_81 (not_81_out, b0);
  not not_82 (not_82_out, b3);
  not not_83 (not_83_out, b0);
  not not_84 (not_84_out, b3);
  not not_85 (not_85_out, b0);
  not not_86 (not_86_out, b4);
  not not_87 (not_87_out, b0);
  not not_88 (not_88_out, b5);
  not not_89 (not_89_out, b1);
  not not_90 (not_90_out, b2);
  not not_91 (not_91_out, b1);
  not not_92 (not_92_out, b2);
  not not_93 (not_93_out, b1);
  not not_94 (not_94_out, b2);
  not not_95 (not_95_out, b1);
  not not_96 (not_96_out, b3);
  not not_97 (not_97_out, b1);
  not not_98 (not_98_out, b3);
  not not_99 (not_99_out, b1);
  not not_100 (not_100_out, b4);
  not not_101 (not_101_out, b1);
  not not_102 (not_102_out, b5);
  not not_103 (not_103_out, b2);
  not not_104 (not_104_out, b3);
  not not_105 (not_105_out, b2);
  not not_106 (not_106_out, b3);
  not not_107 (not_107_out, b2);
  not not_108 (not_108_out, b4);
  not not_109 (not_109_out, b2);
  not not_110 (not_110_out, b5);
  not not_111 (not_111_out, b3);
  not not_112 (not_112_out, b4);
  not not_113 (not_113_out, b3);
  not not_114 (not_114_out, b5);
  not not_115 (not_115_out, b4);
  not not_116 (not_116_out, b5);
  not not_117 (not_117_out, b0);
  not not_118 (not_118_out, b1);
  not not_119 (not_119_out, b2);
  not not_120 (not_120_out, b3);
  not not_121 (not_121_out, b4);
  not not_122 (not_122_out, b0);
  not not_123 (not_123_out, b1);
  not not_124 (not_124_out, b2);
  not not_125 (not_125_out, b3);
  not not_126 (not_126_out, b5);
  not not_127 (not_127_out, b0);
  not not_128 (not_128_out, b1);
  not not_129 (not_129_out, b2);
  not not_130 (not_130_out, b4);
  not not_131 (not_131_out, b5);
  not not_132 (not_132_out, b0);
  not not_133 (not_133_out, b1);
  not not_134 (not_134_out, b2);
  not not_135 (not_135_out, b0);
  not not_136 (not_136_out, b1);
  not not_137 (not_137_out, b3);
  not not_138 (not_138_out, b4);
  not not_139 (not_139_out, b5);
  not not_140 (not_140_out, b0);
  not not_141 (not_141_out, b1);
  not not_142 (not_142_out, b3);
  not not_143 (not_143_out, b0);
  not not_144 (not_144_out, b1);
  not not_145 (not_145_out, b4);
  not not_146 (not_146_out, b0);
  not not_147 (not_147_out, b1);
  not not_148 (not_148_out, b5);
  not not_149 (not_149_out, b0);
  not not_150 (not_150_out, b2);
  not not_151 (not_151_out, b3);
  not not_152 (not_152_out, b4);
  not not_153 (not_153_out, b5);
  not not_154 (not_154_out, b0);
  not not_155 (not_155_out, b2);
  not not_156 (not_156_out, b3);
  not not_157 (not_157_out, b0);
  not not_158 (not_158_out, b2);
  not not_159 (not_159_out, b4);
  not not_160 (not_160_out, b0);
  not not_161 (not_161_out, b2);
  not not_162 (not_162_out, b5);
  not not_163 (not_163_out, b0);
  not not_164 (not_164_out, b3);
  not not_165 (not_165_out, b4);
  not not_166 (not_166_out, b0);
  not not_167 (not_167_out, b3);
  not not_168 (not_168_out, b5);
  not not_169 (not_169_out, b0);
  not not_170 (not_170_out, b4);
  not not_171 (not_171_out, b5);
  not not_172 (not_172_out, b0);
  not not_173 (not_173_out, b1);
  not not_174 (not_174_out, b2);
  not not_175 (not_175_out, b3);
  not not_176 (not_176_out, b4);
  not not_177 (not_177_out, b5);
  not not_178 (not_178_out, b1);
  not not_179 (not_179_out, b2);
  not not_180 (not_180_out, b3);
  not not_181 (not_181_out, b1);
  not not_182 (not_182_out, b2);
  not not_183 (not_183_out, b4);
  not not_184 (not_184_out, b1);
  not not_185 (not_185_out, b2);
  not not_186 (not_186_out, b5);
  not not_187 (not_187_out, b1);
  not not_188 (not_188_out, b3);
  not not_189 (not_189_out, b4);
  not not_190 (not_190_out, b1);
  not not_191 (not_191_out, b3);
  not not_192 (not_192_out, b5);
  not not_193 (not_193_out, b1);
  not not_194 (not_194_out, b4);
  not not_195 (not_195_out, b5);
  not not_196 (not_196_out, b1);
  not not_197 (not_197_out, b2);
  not not_198 (not_198_out, b3);
  not not_199 (not_199_out, b4);
  not not_200 (not_200_out, b2);
  not not_201 (not_201_out, b3);
  not not_202 (not_202_out, b5);
  not not_203 (not_203_out, b2);
  not not_204 (not_204_out, b4);
  not not_205 (not_205_out, b5);
  not not_206 (not_206_out, b2);
  not not_207 (not_207_out, b3);
  not not_208 (not_208_out, b4);
  not not_209 (not_209_out, b5);
  not not_210 (not_210_out, b3);
  not not_211 (not_211_out, b4);
  not not_212 (not_212_out, b5);
  and and_1 (ZF, b0, b1, b2, b3, b4, b5);
  and and_2 (and_2_out, not_1_out, not_2_out, not_3_out, not_4_out);
  and and_3 (and_3_out, not_5_out, not_6_out, not_7_out, not_8_out);
  and and_4 (and_4_out, not_9_out, not_10_out, not_11_out, not_12_out);
  and and_5 (and_5_out, not_13_out, not_14_out, not_15_out, not_16_out);
  and and_6 (and_6_out, not_17_out, not_18_out, not_19_out, not_20_out);
  and and_7 (and_7_out, not_21_out, not_22_out, not_23_out, not_24_out);
  and and_8 (and_8_out, not_25_out, not_26_out, not_27_out, not_28_out);
  and and_9 (and_9_out, not_29_out, not_30_out, not_31_out, not_32_out);
  and and_10 (and_10_out, not_33_out, not_34_out, not_35_out, not_36_out);
  and and_11 (and_11_out, not_37_out, not_38_out, not_39_out, not_40_out);
  and and_12 (and_12_out, not_41_out, not_42_out, not_43_out, not_44_out);
  and and_13 (and_13_out, not_45_out, not_46_out, not_47_out, not_48_out);
  and and_14 (and_14_out, not_49_out, not_50_out, not_51_out, not_52_out);
  and and_15 (and_15_out, not_53_out, not_54_out, not_55_out, not_56_out);
  and and_16 (and_16_out, not_57_out, not_58_out, not_59_out, not_60_out);
  and and_17 (and_17_out, not_61_out, not_62_out, not_63_out, not_64_out, not_65_out, not_66_out);
  and and_18 (and_18_out, not_67_out, not_68_out, b3, b4, b5);
  and and_19 (and_19_out, not_69_out, not_70_out, b2, b4, b5);
  and and_20 (and_20_out, not_71_out, not_72_out, b2, b3, b5);
  and and_21 (and_21_out, not_73_out, not_74_out, b2, b3, b4);
  and and_22 (and_22_out, not_75_out, b1, not_76_out, b4, b5);
  and and_23 (and_23_out, not_77_out, b1, not_78_out, b3, b5);
  and and_24 (and_24_out, not_79_out, b1, not_80_out, b3, b4);
  and and_25 (and_25_out, not_81_out, b1, b2, not_82_out, b5);
  and and_26 (and_26_out, not_83_out, b1, b2, not_84_out, b4);
  and and_27 (and_27_out, not_85_out, b1, b2, b3, not_86_out);
  and and_28 (and_28_out, not_87_out, b1, b2, b3, not_88_out);
  and and_29 (and_29_out, b0, not_89_out, not_90_out, b4, b5);
  and and_30 (and_30_out, b0, not_91_out, not_92_out, b3, b5);
  and and_31 (and_31_out, b0, not_93_out, not_94_out, b3, b4);
  and and_32 (and_32_out, b0, not_95_out, b2, not_96_out, b5);
  and and_33 (and_33_out, b0, not_97_out, b2, not_98_out, b4);
  and and_34 (and_34_out, b0, not_99_out, b2, b3, not_100_out);
  and and_35 (and_35_out, b0, not_101_out, b2, b3, not_102_out);
  and and_36 (and_36_out, b0, b1, not_103_out, not_104_out, b5);
  and and_37 (and_37_out, b0, b1, not_105_out, not_106_out, b4);
  and and_38 (and_38_out, b0, b1, not_107_out, b3, not_108_out);
  and and_39 (and_39_out, b0, b1, not_109_out, b3, not_110_out);
  and and_40 (and_40_out, b0, b1, b2, not_111_out, not_112_out);
  and and_41 (and_41_out, b0, b1, b2, not_113_out, not_114_out);
  and and_42 (and_42_out, b0, b1, b2, not_115_out, not_116_out);
  and and_43 (and_43_out, not_117_out, not_118_out, not_119_out, not_120_out, not_121_out, b5);
  and and_44 (and_44_out, not_122_out, not_123_out, not_124_out, not_125_out, b4, not_126_out);
  and and_45 (and_45_out, not_127_out, not_128_out, not_129_out, b3, not_130_out, not_131_out);
  and and_46 (and_46_out, not_132_out, not_133_out, not_134_out, b3, b4, b5);
  and and_47 (and_47_out, not_135_out, not_136_out, b2, not_137_out, not_138_out, not_139_out);
  and and_48 (and_48_out, not_140_out, not_141_out, b2, not_142_out, b4, b5);
  and and_49 (and_49_out, not_143_out, not_144_out, b2, b3, not_145_out, b5);
  and and_50 (and_50_out, not_146_out, not_147_out, b2, b3, b4, not_148_out);
  and and_51 (and_51_out, not_149_out, b1, not_150_out, not_151_out, not_152_out, not_153_out);
  and and_52 (and_52_out, not_154_out, b1, not_155_out, not_156_out, b4, b5);
  and and_53 (and_53_out, not_157_out, b1, not_158_out, b3, not_159_out, b5);
  and and_54 (and_54_out, not_160_out, b1, not_161_out, b3, b4, not_162_out);
  and and_55 (and_55_out, not_163_out, b1, b2, not_164_out, not_165_out, b5);
  and and_56 (and_56_out, not_166_out, b1, b2, not_167_out, b4, not_168_out);
  and and_57 (and_57_out, not_169_out, b1, b2, b3, not_170_out, not_171_out);
  and and_58 (and_58_out, not_172_out, b1, b2, b3, b4, b5);
  and and_59 (and_59_out, b0, not_173_out, not_174_out, not_175_out, not_176_out, not_177_out);
  and and_60 (and_60_out, b0, not_178_out, not_179_out, not_180_out, b4, b5);
  and and_61 (and_61_out, b0, not_181_out, not_182_out, b3, not_183_out, b5);
  and and_62 (and_62_out, b0, not_184_out, not_185_out, b3, b4, not_186_out);
  and and_63 (and_63_out, b0, not_187_out, b2, not_188_out, not_189_out, b5);
  and and_64 (and_64_out, b0, not_190_out, b2, not_191_out, b4, not_192_out);
  and and_65 (and_65_out, b0, not_193_out, b2, b3, not_194_out, not_195_out);
  and and_66 (and_66_out, b0, not_196_out, b2, b3, b4, b5);
  and and_67 (and_67_out, b0, b1, not_197_out, not_198_out, not_199_out, b5);
  and and_68 (and_68_out, b0, b1, not_200_out, not_201_out, b4, not_202_out);
  and and_69 (and_69_out, b0, b1, not_203_out, b3, not_204_out, not_205_out);
  and and_70 (and_70_out, b0, b1, not_206_out, b3, b4, b5);
  and and_71 (and_71_out, b0, b1, b2, not_207_out, not_208_out, not_209_out);
  and and_72 (and_72_out, b0, b1, b2, not_210_out, b4, b5);
  and and_73 (and_73_out, b0, b1, b2, b3, not_211_out, b5);
  and and_74 (and_74_out, b0, b1, b2, b3, b4, not_212_out);
  or or_1 (s3, and_2_out, and_3_out, and_4_out, and_5_out, and_6_out, and_7_out, and_8_out, and_9_out, and_10_out, and_11_out, and_12_out, and_13_out, and_14_out, and_15_out, and_16_out);
  or or_2 (s4, and_17_out, and_18_out, and_19_out, and_20_out, and_21_out, and_22_out, and_23_out, and_24_out, and_25_out, and_26_out, and_27_out, and_28_out, and_29_out, and_30_out, and_31_out, and_32_out, and_33_out, and_34_out, and_35_out, and_36_out, and_37_out, and_38_out, and_39_out, and_40_out, and_41_out, and_42_out);
  or or_3 (s5, and_43_out, and_44_out, and_45_out, and_46_out, and_47_out, and_48_out, and_49_out, and_50_out, and_51_out, and_52_out, and_53_out, and_54_out, and_55_out, and_56_out, and_57_out, and_58_out, and_59_out, and_60_out, and_61_out, and_62_out, and_63_out, and_64_out, and_65_out, and_66_out, and_67_out, and_68_out, and_69_out, and_70_out, and_71_out, and_72_out, and_73_out, and_74_out);

  assign BAF = 1'b0;
  assign INV_OP = 1'b1;
  assign s0 = 1'b0;
  assign s1 = 1'b0;
  assign s2 = 1'b0;
endmodule

module OP1 (
  input  x0,
  input  x1,
  input  x2,
  input  x3,
  input  x4,
  input  x5,
  input  b0,
  input  b1,
  input  b2,
  input  b3,
  input  b4,
  input  b5,
  output [5:0] out_13,
  output s5,
  output [5:0] out_15,
  output BAF,
  output s0,
  output s1,
  output s2,
  output s3,
  output s4,
  output ZF,
  output INV_OP
);

  wire comparator_1_eq, comparator_1_lt, not_1_out, not_2_out, VLD_2_s5, VLD_s5;

  not not_1 (not_1_out, VLD_s5);
  and and_1 (BAF, not_1_out, not_2_out);
  VLD VLD (
    .b0(x0), .b1(x1), .b2(x2), .b3(x3), .b4(x4), .b5(x5), .s5(VLD_s5));  // open: s0, s1, s2, s3, s4, ZF, BAF, INV_OP
  not not_2 (not_2_out, VLD_2_s5);
  VLD VLD_2 (
    .b0(b0), .b1(b1), .b2(b2), .b3(b3), .b4(b4), .b5(b5), .s5(VLD_2_s5));  // open: s0, s1, s2, s3, s4, ZF, BAF, INV_OP
  Comparator #(.width(6), .mode("unsigned")) comparator_1 (
    .a({b0, b1, b2, b3, b4, b5}), .b({x0, x1, x2, x3, x4, x5}), .eq(comparator_1_eq), .lt(comparator_1_lt));  // open: gt
  or or_1 (s5, comparator_1_eq, comparator_1_lt);

  assign INV_OP = 1'b1;
  assign out_13 = {b0, b1, b2, b3, b4, b5};
  assign out_15 = {x0, x1, x2, x3, x4, x5};
  assign s0 = 1'b0;
  assign s1 = 1'b0;
  assign s2 = 1'b0;
  assign s3 = 1'b0;
  assign s4 = 1'b0;
  assign ZF = 1'b0;
endmodule

module OP2 (
  input  b0,
  input  b1,
  input  b2,
  input  b3,
  input  b4,
  input  b5,
  input  x0,
  input  x1,
  input  x2,
  input  x3,
  input  x4,
  input  x5,
  output s0,
  output s1,
  output s2,
  output s3,
  output s4,
  output s5,
  output ZF,
  output BAF,
  output INV_OP
);

  wire not_1_out, not_2_out, VLD_2_s5, VLD_s5;
  wire [5:0] NEG_s0, XNOR_out;

  VLD VLD (
    .b0(b0), .b1(b1), .b2(b2), .b3(b3), .b4(b4), .b5(b5), .s5(VLD_s5));  // open: s0, s1, s2, s3, s4, ZF, BAF, INV_OP
  not not_1 (not_1_out, VLD_s5);
  not not_2 (not_2_out, VLD_2_s5);
  and and_1 (BAF, not_1_out, not_2_out);
  VLD VLD_2 (
    .b0(x0), .b1(x1), .b2(x2), .b3(x3), .b4(x4), .b5(x5), .s5(VLD_2_s5));  // open: s0, s1, s2, s3, s4, ZF, BAF, INV_OP
  assign XNOR_out = ~({b5, b4, b3, b2, b1, b0} ^ NEG_s0);  // XNOR_Gate XNOR, 6 bits wide
  and and_2 (s5, XNOR_out[5], XNOR_out[4], XNOR_out[3], XNOR_out[2], XNOR_out[1], XNOR_out[0]);
  NEG NEG (
    .b0(x0), .b1(x1), .b2(x2), .b3(x3), .b4(x4), .b5(x5), .s0(NEG_s0[0]), .s1(NEG_s0[1]), .s2(NEG_s0[2]),
    .s3(NEG_s0[3]), .s4(NEG_s0[4]), .s5(NEG_s0[5]));  // open: ZF, BAF, INV_OP

  assign INV_OP = 1'b1;
  assign s0 = 1'b0;
  assign s1 = 1'b0;
  assign s2 = 1'b0;
  assign s3 = 1'b0;
  assign s4 = 1'b0;
  assign ZF = 1'b0;
endmodule

module OP3 (
  input  b0,
  input  b1,
  input  b2,
  input  b3,
  input  b4,
  input  b5,
  output s0,
  output s1,
  output s2,
  output s3,
  output s4,
  output s5,
  output ZF,
  output BAF,
  output INV_OP
);

  wire and_1_out, and_2_out, and_3_out, and_4_out, and_5_out, and_6_out, and_7_out, and_8_out, and_9_out,
       and_10_out, and_11_out, and_12_out, and_13_out, and_14_out, and_15_out, and_16_out, and_17_out,
       and_18_out, and_19_out, and_20_out, and_21_out, and_22_out, and_23_out, and_24_out, and_25_out,
       and_26_out, and_27_out, and_28_out, and_29_out, and_30_out, and_31_out, and_32_out, and_33_out,
       and_34_out, and_35_out, and_36_out, and_37_out, and_38_out, and_39_out, and_40_out, and_41_out,
       and_42_out, and_43_out, and_44_out, and_45_out, and_46_out, and_47_out, and_48_out, and_49_out,
       and_50_out, and_51_out, and_52_out, and_53_out, and_54_out, and_55_out, and_56_out, and_57_out,
       and_58_out, and_59_out, and_60_out, and_61_out, and_62_out, and_63_out, and_64_out, not_1_out,
       not_2_out, not_3_out, not_4_out, not_5_out, not_6_out, not_7_out, not_8_out, not_9_out, not_10_out,
       not_11_out, not_12_out, not_13_out, not_14_out, not_15_out, not_16_out, not_17_out, not_18_out,
       not_19_out, not_20_out, not_21_out, not_22_out, not_23_out, not_24_out, not_25_out, not_26_out,
       not_27_out, not_28_out, not_29_out, not_30_out, not_31_out, not_32_out, not_33_out, not_34_out,
       not_35_out, not_36_out, not_37_out, not_38_out, not_39_out, not_40_out, not_41_out, not_42_out,
       not_43_out, not_44_out, not_45_out, not_46_out, not_47_out, not_48_out, not_49_out, not_50_out,
       not_51_out, not_52_out, not_53_out, not_54_out, not_55_out, not_56_out, not_57_out, not_58_out,
       not_59_out, not_60_out, not_61_out, not_62_out, not_63_out, not_64_out, not_65_out, not_66_out,
       not_67_out, not_68_out, not_69_out, not_70_out, not_71_out, not_72_out, not_73_out, not_74_out,
       not_75_out, not_76_out, not_77_out, not_78_out, not_79_out, not_80_out, not_81_out, not_82_out,
       not_83_out, not_84_out, not_85_out, not_86_out, not_87_out, not_88_out, not_89_out, not_90_out,
       not_91_out, not_92_out, not_93_out, not_94_out, not_95_out, not_96_out, not_97_out, not_98_out,
       not_99_out, not_100_out, not_101_out, not_102_out, not_103_out, not_104_out, not_105_out, not_106_out,
       not_107_out, not_108_out, not_109_out, not_110_out, not_111_out, not_112_out, not_113_out,
       not_114_out, not_115_out, not_116_out, not_117_out, not_118_out, not_119_out, not_120_out,
       not_121_out, not_122_out, not_123_out, not_124_out, not_125_out, not_126_out, not_127_out,
       not_128_out, not_129_out, not_130_out, not_131_out, not_132_out, not_133_out, not_134_out,
       not_135_out, not_136_out, not_137_out, not_138_out, not_139_out, not_140_out, not_141_out,
       not_142_out, not_143_out, not_144_out, not_145_out, not_146_out, not_147_out, not_148_out,
       not_149_out, not_150_out, not_151_out, not_152_out, not_153_out, not_154_out, not_155_out,
       not_156_out, not_157_out, not_158_out;

  not not_1 (not_1_out, b0);
  not not_2 (not_2_out, b1);
  not not_3 (not_3_out, b2);
  not not_4 (not_4_out, b3);
  not not_5 (not_5_out, b5);
  not not_6 (not_6_out, b0);
  not not_7 (not_7_out, b1);
  not not_8 (not_8_out, b2);
  not not_9 (not_9_out, b4);
  not not_10 (not_10_out, b5);
  not not_11 (not_11_out, b0);
  not not_12 (not_12_out, b1);
  not not_13 (not_13_out, b4);
  not not_14 (not_14_out, b0);
  not not_15 (not_15_out, b2);
  not not_16 (not_16_out, b5);
  not not_17 (not_17_out, b1);
  not not_18 (not_18_out, b2);
  not not_19 (not_19_out, b4);
  not not_20 (not_20_out, b1);
  not not_21 (not_21_out, b3);
  not not_22 (not_22_out, b5);
  not not_23 (not_23_out, b1);
  not not_24 (not_24_out, b2);
  not not_25 (not_25_out, b3);
  not not_26 (not_26_out, b4);
  not not_27 (not_27_out, b5);
  not not_28 (not_28_out, b0);
  not not_29 (not_29_out, b1);
  not not_30 (not_30_out, b2);
  not not_31 (not_31_out, b5);
  not not_32 (not_32_out, b0);
  not not_33 (not_33_out, b3);
  not not_34 (not_34_out, b5);
  not not_35 (not_35_out, b0);
  not not_36 (not_36_out, b0);
  not not_37 (not_37_out, b2);
  not not_38 (not_38_out, b3);
  not not_39 (not_39_out, b0);
  not not_40 (not_40_out, b3);
  not not_41 (not_41_out, b0);
  not not_42 (not_42_out, b0);
  not not_43 (not_43_out, b4);
  not not_44 (not_44_out, b5);
  not not_45 (not_45_out, b3);
  not not_46 (not_46_out, b5);
  not not_47 (not_47_out, b5);
  not not_48 (not_48_out, b1);
  not not_49 (not_49_out, b2);
  not not_50 (not_50_out, b3);
  not not_51 (not_51_out, b1);
  not not_52 (not_52_out, b4);
  not not_53 (not_53_out, b5);
  not not_54 (not_54_out, b3);
  not not_55 (not_55_out, b4);
  not not_56 (not_56_out, b5);
  not not_57 (not_57_out, b2);
  not not_58 (not_58_out, b4);
  not not_59 (not_59_out, b0);
  not not_60 (not_60_out, b1);
  not not_61 (not_61_out, b2);
  not not_62 (not_62_out, b0);
  not not_63 (not_63_out, b1);
  not not_64 (not_64_out, b2);
  not not_65 (not_65_out, b0);
  not not_66 (not_66_out, b1);
  not not_67 (not_67_out, b2);
  not not_68 (not_68_out, b0);
  not not_69 (not_69_out, b3);
  not not_70 (not_70_out, b4);
  not not_71 (not_71_out, b5);
  not not_72 (not_72_out, b1);
  not not_73 (not_73_out, b5);
  not not_74 (not_74_out, b5);
  not not_75 (not_75_out, b0);
  not not_76 (not_76_out, b2);
  not not_77 (not_77_out, b4);
  not not_78 (not_78_out, b0);
  not not_79 (not_79_out, b1);
  not not_80 (not_80_out, b2);
  not not_81 (not_81_out, b3);
  not not_82 (not_82_out, b4);
  not not_83 (not_83_out, b1);
  not not_84 (not_84_out, b3);
  not not_85 (not_85_out, b3);
  not not_86 (not_86_out, b1);
  not not_87 (not_87_out, b4);
  not not_88 (not_88_out, b2);
  not not_89 (not_89_out, b3);
  not not_90 (not_90_out, b5);
  not not_91 (not_91_out, b2);
  not not_92 (not_92_out, b4);
  not not_93 (not_93_out, b5);
  not not_94 (not_94_out, b2);
  not not_95 (not_95_out, b1);
  not not_96 (not_96_out, b2);
  not not_97 (not_97_out, b3);
  not not_98 (not_98_out, b1);
  not not_99 (not_99_out, b2);
  not not_100 (not_100_out, b4);
  not not_101 (not_101_out, b5);
  not not_102 (not_102_out, b0);
  not not_103 (not_103_out, b3);
  not not_104 (not_104_out, b5);
  not not_105 (not_105_out, b0);
  not not_106 (not_106_out, b1);
  not not_107 (not_107_out, b0);
  not not_108 (not_108_out, b2);
  not not_109 (not_109_out, b4);
  not not_110 (not_110_out, b5);
  not not_111 (not_111_out, b2);
  not not_112 (not_112_out, b4);
  not not_113 (not_113_out, b0);
  not not_114 (not_114_out, b3);
  not not_115 (not_115_out, b1);
  not not_116 (not_116_out, b2);
  not not_117 (not_117_out, b4);
  not not_118 (not_118_out, b2);
  not not_119 (not_119_out, b3);
  not not_120 (not_120_out, b4);
  not not_121 (not_121_out, b1);
  not not_122 (not_122_out, b3);
  not not_123 (not_123_out, b4);
  not not_124 (not_124_out, b5);
  not not_125 (not_125_out, b5);
  not not_126 (not_126_out, b0);
  not not_127 (not_127_out, b1);
  not not_128 (not_128_out, b2);
  not not_129 (not_129_out, b0);
  not not_130 (not_130_out, b3);
  not not_131 (not_131_out, b1);
  not not_132 (not_132_out, b3);
  not not_133 (not_133_out, b4);
  not not_134 (not_134_out, b0);
  not not_135 (not_135_out, b5);
  not not_136 (not_136_out, b0);
  not not_137 (not_137_out, b5);
  not not_138 (not_138_out, b0);
  not not_139 (not_139_out, b2);
  not not_140 (not_140_out, b4);
  not not_141 (not_141_out, b5);
  not not_142 (not_142_out, b1);
  not not_143 (not_143_out, b2);
  not not_144 (not_144_out, b3);
  not not_145 (not_145_out, b1);
  not not_146 (not_146_out, b3);
  not not_147 (not_147_out, b4);
  not not_148 (not_148_out, b4);
  not not_149 (not_149_out, b5);
  not not_150 (not_150_out, b0);
  not not_151 (not_151_out, b1);
  not not_152 (not_152_out, b2);
  not not_153 (not_153_out, b3);
  not not_154 (not_154_out, b4);
  not not_155 (not_155_out, b5);
  not not_156 (not_156_out, b1);
  not not_157 (not_157_out, b2);
  not not_158 (not_158_out, b5);
  and and_1 (and_1_out, not_1_out, not_2_out, not_3_out, not_4_out, b4, not_5_out);
  and and_2 (and_2_out, not_6_out, not_7_out, not_8_out, b3, not_9_out, not_10_out);
  and and_3 (and_3_out, not_11_out, not_12_out, b2, not_13_out, b5);
  and and_4 (and_4_out, not_14_out, b1, not_15_out, b3, b4, not_16_out);
  and and_5 (and_5_out, b0, not_17_out, not_18_out, b3, not_19_out, b5);
  and and_6 (and_6_out, b0, not_20_out, b2, not_21_out, not_22_out);
  and and_7 (and_7_out, b0, not_23_out, b2, b3, b4, b5);
  and and_8 (and_8_out, b0, b1, not_24_out, not_25_out, b4, b5);
  and and_9 (and_9_out, b0, b1, b2, b3, not_26_out, not_27_out);
  and and_10 (and_10_out, not_28_out, not_29_out, not_30_out, b3, b4, not_31_out);
  and and_11 (and_11_out, not_32_out, b2, not_33_out, b4, not_34_out);
  and and_12 (and_12_out, not_35_out, b2, b3, b4, b5);
  and and_13 (and_13_out, not_36_out, b1, not_37_out, not_38_out, b5);
  and and_14 (and_14_out, not_39_out, b1, not_40_out, b4);
  and and_15 (and_15_out, not_41_out, b1, b4, b5);
  and and_16 (and_16_out, not_42_out, b1, b3, not_43_out, not_44_out);
  and and_17 (and_17_out, b1, b2, not_45_out, not_46_out);
  and and_18 (and_18_out, b1, b2, b4, not_47_out);
  and and_19 (and_19_out, b0, not_48_out, not_49_out, not_50_out, b5);
  and and_20 (and_20_out, b0, not_51_out, b2, b3, not_52_out, not_53_out);
  and and_21 (and_21_out, b0, b1, not_54_out, not_55_out, not_56_out);
  and and_22 (and_22_out, b0, b1, not_57_out, b3, b5);
  and and_23 (and_23_out, b0, b1, b2, not_58_out, b5);
  and and_24 (and_24_out, not_59_out, not_60_out, not_61_out, b4, b5);
  and and_25 (and_25_out, not_62_out, not_63_out, not_64_out, b3, b5);
  and and_26 (and_26_out, not_65_out, not_66_out, not_67_out, b3, b4);
  and and_27 (and_27_out, not_68_out, b2, not_69_out, not_70_out, not_71_out);
  and and_28 (and_28_out, not_72_out, b2, b3, not_73_out);
  and and_29 (and_29_out, b2, b3, b4, not_74_out);
  and and_30 (and_30_out, not_75_out, b1, not_76_out, not_77_out, b5);
  and and_31 (and_31_out, not_78_out, b1, b2, b4);
  and and_32 (and_32_out, b0, not_79_out, not_80_out, not_81_out, not_82_out);
  and and_33 (and_33_out, b0, not_83_out, b2, not_84_out, b5);
  and and_34 (and_34_out, b0, b2, not_85_out, b4, b5);
  and and_35 (and_35_out, b0, not_86_out, b2, b3, not_87_out);
  and and_36 (and_36_out, b0, b1, not_88_out, not_89_out, b4, not_90_out);
  and and_37 (and_37_out, b0, b1, not_91_out, b3, not_92_out, not_93_out);
  and and_38 (and_38_out, b0, b1, not_94_out, b3, b4, b5);
  and and_39 (and_39_out, not_95_out, not_96_out, not_97_out, b4, b5);
  and and_40 (and_40_out, not_98_out, not_99_out, b3, not_100_out, not_101_out);
  and and_41 (and_41_out, not_102_out, b2, not_103_out, not_104_out);
  and and_42 (and_42_out, not_105_out, not_106_out, b2, b4, b5);
  and and_43 (and_43_out, not_107_out, b1, not_108_out, not_109_out, not_110_out);
  and and_44 (and_44_out, b1, not_111_out, b3, not_112_out, b5);
  and and_45 (and_45_out, not_113_out, b1, b2, not_114_out);
  and and_46 (and_46_out, b0, not_115_out, not_116_out, not_117_out);
  and and_47 (and_47_out, b0, not_118_out, not_119_out, not_120_out);
  and and_48 (and_48_out, b0, not_121_out, not_122_out, not_123_out, b5);
  and and_49 (and_49_out, b0, b2, b4, not_124_out);
  and and_50 (and_50_out, b0, b1, b3, b4, not_125_out);
  and and_51 (and_51_out, b0, b1, b2, b4);
  and and_52 (and_52_out, not_126_out, not_127_out, not_128_out, b4, b5);
  and and_53 (and_53_out, not_129_out, not_130_out, b4, b5);
  and and_54 (and_54_out, not_131_out, b2, not_132_out, not_133_out, b5);
  and and_55 (and_55_out, not_134_out, b2, b4, not_135_out);
  and and_56 (and_56_out, not_136_out, b1, b4, not_137_out);
  and and_57 (and_57_out, not_138_out, b1, b2, b3, b5);
  and and_58 (and_58_out, b0, not_139_out, not_140_out, not_141_out);
  and and_59 (and_59_out, b0, not_142_out, not_143_out, not_144_out, b4);
  and and_60 (and_60_out, b0, not_145_out, b2, b3, b5);
  and and_61 (and_61_out, b0, b1, not_146_out, not_147_out);
  and and_62 (and_62_out, b0, b1, not_148_out, not_149_out);
  and and_63 (and_63_out, not_150_out, not_151_out, not_152_out, not_153_out, not_154_out, not_155_out);
  and and_64 (and_64_out, b0, not_156_out, not_157_out, b3, b4, not_158_out);
  or or_1 (s0, and_1_out, and_2_out, and_3_out, and_4_out, and_5_out, and_6_out, and_7_out, and_8_out, and_9_out);
  or or_2 (s4, and_52_out, and_53_out, and_54_out, and_55_out, and_56_out, and_57_out, and_58_out, and_59_out, and_60_out, and_61_out, and_62_out);
  or or_3 (ZF, and_63_out, and_64_out);
  or or_4 (s1, and_10_out, and_11_out, and_12_out, and_13_out, and_14_out, and_15_out, and_16_out, and_17_out, and_18_out, and_19_out, and_20_out, and_21_out, and_22_out, and_23_out);
  or or_5 (s2, and_24_out, and_25_out, and_26_out, and_27_out, and_28_out, and_29_out, and_30_out, and_31_out, and_32_out, and_33_out, and_34_out, and_35_out, and_36_out, and_37_out, and_38_out);
  or or_6 (s3, and_39_out, and_40_out, and_41_out, and_42_out, and_43_out, and_44_out, and_45_out, and_46_out, and_47_out, and_48_out, and_49_out, and_50_out, and_51_out);

  assign BAF = 1'b0;
  assign INV_OP = 1'b1;
  assign s5 = b5;
endmodule

module test (
);

  wire alu_1_p1;

  // ALU alu_1: pin names not known; wires that end beside it: alu_1_p1
endmodule
