// Logisim project upgraded_CPU.circ as structural Verilog: 5 circuits, main circuit main
module main (
  input  in_1,
  input  in_2,
  output [5:0] X,
  output [5:0] Y,
  output [4:0] Command,
  output [5:0] Output_ALU,
  output [5:0] IR_Reg,
  output [5:0] IR_Code,
  output INV_OP,
  output [5:0] out_10,
  output [5:0] Values,
  output [5:0] out_12,
  output [5:0] out_13,
  output [5:0] out_14,
  output [5:0] out_15,
  output [5:0] out_16,
  output [5:0] out_17,
  output [2:0] sregsel,
  output [2:0] dregsel
);

  wire BAF, clock_1_out, clock_2_out, clock_3_out, clock_4_out, clock_5_out, dwrite, imload, irload, pcload,
       pcsel, readwrite, ZF;
  wire [1:0] addrsel, regsel;
  wire [5:0] dval, multiplexer_3_out, pc_inc_1_pc_out, RAM_ADDRESS, RAM_DATA, register_3_q, register_4_q;

  Clock clock_1 (.out(clock_1_out));
  Register #(.width(6)) register_1 (.D(RAM_DATA), .en(irload), .Q(IR_Reg), .clk(clock_1_out));  // open: clr
  Multiplexer #(.select(2), .width(6), .enable("false")) multiplexer_1 (
    .in0(register_4_q), .in1(register_3_q), .in2(Y), .in3(X), .out(RAM_ADDRESS), .sel(addrsel));
  Clock clock_2 (.out(clock_2_out));
  Clock clock_3 (.out(clock_3_out));
  RAM #(.addrWidth(6), .dataWidth(6), .bus("separate")) ram_1 (
    .addr(RAM_ADDRESS), .din(X), .data(RAM_DATA), .str(readwrite), .clk(clock_2_out));  // open: sel, ld, clr
  Register #(.width(6)) register_2 (.D(IR_Reg), .en(irload), .Q(IR_Code), .clk(clock_3_out));  // open: clr
  Register #(.width(6)) register_3 (.D(RAM_DATA), .en(imload), .Q(register_3_q), .clk(clock_4_out));  // open: clr
  Clock clock_4 (.out(clock_4_out));
  Registers registers_1 (
    .dval(dval), .dregsel(dregsel), .dbus(X), .sbus(Y), .sregsel(sregsel), .dwrite(dwrite), .R0(out_10),
    .R1(out_12), .R2(out_14), .R3(out_16), .R4(Values), .R5(out_13), .R6(out_15), .R7(out_17));
  ALU alu_1 (.Answer(Output_ALU), .ZF(ZF), .BAF(BAF), .INV_OP(INV_OP), .Y(Y), .X(X), .Input(Command));
  Multiplexer #(.select(2), .width(6), .enable("false")) multiplexer_2 (
    .in0(register_3_q), .in1(Y), .in2(RAM_DATA), .in3(Output_ALU), .out(dval), .sel(regsel));
  Multiplexer #(.width(6), .enable("false")) multiplexer_3 (
    .in0(register_3_q), .in1(pc_inc_1_pc_out), .out(multiplexer_3_out), .sel(pcsel));
  PC_Inc pc_inc_1 (.PC_in(register_4_q), .PC_out(pc_inc_1_pc_out));
  Register #(.width(6)) register_4 (
    .D(multiplexer_3_out), .en(pcload), .Q(register_4_q), .clk(clock_5_out));  // open: clr
  Clock clock_5 (.out(clock_5_out));
  Decoder decoder_1 (
    .dregsel(dregsel), .sregsel(sregsel), .aluop(Command), .IR_Code(IR_Code), .IR_Reg(IR_Reg),
    .irload(irload), .imload(imload), .addrsel(addrsel), .pcload(pcload), .readwrite(readwrite),
    .regsel(regsel), .dwrite(dwrite), .pcsel(pcsel), .ZF(ZF), .BAF(BAF));  // open: operation, out_8

  // Other names for the same wires on the sheet: aluop[4:0] = Command; dbus[5:0] = X; IRCode[5:0] = IR_Code;
  //   IRReg[5:0] = IR_Reg; OUT_alu[5:0] = Output_ALU; R0[5:0] = out_10; R1[5:0] = out_12; R2[5:0] = out_14;
  //   R3[5:0] = out_16; R4[5:0] = Values; R5[5:0] = out_13; R6[5:0] = out_15; R7[5:0] = out_17; sbus[5:0] = Y

  // Notes on the sheet:
  //   RAM
  //   Immed
  //   ALU
  //   Registers
  //   Process Count
  //   Decoder
endmodule

module Registers (
  input  dwrite,
  input  [2:0] dregsel,
  input  [2:0] sregsel,
  input  [5:0] dval,
  output [5:0] R0,
  output [5:0] R4,
  output [5:0] dbus,
  output [5:0] R1,
  output [5:0] R5,
  output [5:0] R2,
  output [5:0] R6,
  output [5:0] R3,
  output [5:0] R7,
  output [5:0] sbus
);

  wire clock_1_out, demultiplexer_1_out0, demultiplexer_1_out1, demultiplexer_1_out2, demultiplexer_1_out3,
       demultiplexer_1_out4, demultiplexer_1_out5, demultiplexer_1_out6, demultiplexer_1_out7;

  Clock clock_1 (.out(clock_1_out));
  Register #(.width(6)) u_R0 (.D(dval), .en(demultiplexer_1_out0), .Q(R0), .clk(clock_1_out));  // open: clr
  Register #(.width(6)) u_R1 (.D(dval), .en(demultiplexer_1_out1), .Q(R1), .clk(clock_1_out));  // open: clr
  Register #(.width(6)) u_R2 (.D(dval), .en(demultiplexer_1_out2), .Q(R2), .clk(clock_1_out));  // open: clr
  Register #(.width(6)) u_R3 (.D(dval), .en(demultiplexer_1_out3), .Q(R3), .clk(clock_1_out));  // open: clr
  Demultiplexer #(.select(3), .enable("false")) demultiplexer_1 (
    .out0(demultiplexer_1_out0), .out1(demultiplexer_1_out1), .out2(demultiplexer_1_out2),
    .out3(demultiplexer_1_out3), .out4(demultiplexer_1_out4), .out5(demultiplexer_1_out5),
    .out6(demultiplexer_1_out6), .out7(demultiplexer_1_out7), .in(dwrite), .sel(dregsel));
  Register #(.width(6)) u_R4 (.D(dval), .en(demultiplexer_1_out4), .Q(R4), .clk(clock_1_out));  // open: clr
  Register #(.width(6)) u_R5 (.D(dval), .en(demultiplexer_1_out5), .Q(R5), .clk(clock_1_out));  // open: clr
  Register #(.width(6)) u_R6 (.D(dval), .en(demultiplexer_1_out6), .Q(R6), .clk(clock_1_out));  // open: clr
  Register #(.width(6)) u_R7 (.D(dval), .en(demultiplexer_1_out7), .Q(R7), .clk(clock_1_out));  // open: clr
  Multiplexer #(.select(3), .width(6), .enable("false")) multiplexer_1 (
    .in0(R0), .in1(R1), .in2(R2), .in3(R3), .in4(R4), .in5(R5), .in6(R6), .in7(R7), .out(dbus), .sel(dregsel));
  Multiplexer #(.select(3), .width(6), .enable("false")) multiplexer_2 (
    .in0(R0), .in1(R1), .in2(R2), .in3(R3), .in4(R4), .in5(R5), .in6(R6), .in7(R7), .out(sbus), .sel(sregsel));

  // Other names for the same wires on the sheet: drs[2:0] = dregsel

  // Notes on the sheet:
  //   Registers
endmodule

module PC_Inc (
  input  [5:0] PC_in,
  output [5:0] PC_out
);

  Adder #(.width(6)) adder_1 (.a(PC_in), .b(6'b000001), .out(PC_out), .cin(1'b0));  // open: cout

  // Notes on the sheet:
  //   PC Increment
endmodule

module PC_Phase_Counter (
  input  x1,
  input  x2,
  output a1,
  output a2
);

  wire not_1_out;

  and and_1 (a1, x1, x2);
  not not_1 (not_1_out, x2);
  and and_2 (a2, x1, not_1_out);

  // Notes on the sheet:
  //   PC Phase Counter
endmodule

module Decoder (
  input  [5:0] IR_Code,
  input  [5:0] IR_Reg,
  input  ZF,
  input  BAF,
  output [2:0] dregsel,
  output [2:0] sregsel,
  output [4:0] aluop,
  output [1:0] out_8,
  output irload,
  output imload,
  output pcsel,
  output pcload,
  output readwrite,
  output [1:0] regsel,
  output [4:0] operation,
  output dwrite,
  output [1:0] addrsel
);

  wire and_1_out, and_2_out, and_3_out, and_4_out, and_5_out, and_6_out, and_7_out, clock_1_out,
       multiplexer_2_out, multiplexer_4_out, multiplexer_6_out, not_1_out, not_2_out, not_3_out, not_4_out,
       not_5_out, not_6_out, not_7_out, not_8_out, not_9_out, not_10_out, not_11_out, not_12_out, or_1_out,
       or_2_out, or_3_out, or_4_out, or_5_out;
  wire [1:0] counter_1_q, multiplexer_3_out, multiplexer_5_out, multiplexer_7_out, multiplexer_8_out;

  Multiplexer #(.select(2), .enable("false")) multiplexer_1 (
    .in0(1'b1), .in1(1'b0), .in2(1'b0), .in3(1'b0), .out(irload), .sel(out_8));
  or or_1 (or_1_out, IR_Code[2], IR_Code[4]);
  not not_1 (not_1_out, ZF);
  not not_2 (not_2_out, BAF);
  Multiplexer #(.select(5), .enable("false")) multiplexer_2 (
    .in0(1'b0), .in1(1'b1), .in2(1'b0), .in3(1'b1), .in4(1'b1), .in5(1'b0), .in6(1'b0), .in7(1'b0),
    .in8(1'b0), .in9(1'b0), .in10(1'b0), .in11(1'b0), .in12(1'b0), .in13(1'b0), .in14(1'b0), .in15(1'b0),
    .in16(1'b0), .in17(1'b0), .in18(1'b0), .in19(1'b0), .in20(1'b0), .in21(1'b0), .in22(1'b0), .in23(1'b0),
    .in24(1'b0), .in25(1'b0), .in26(1'b0), .in27(1'b0), .in28(1'b0), .in29(1'b0), .in30(1'b0), .in31(1'b1),
    .out(multiplexer_2_out), .sel(IR_Code[4:0]));
  Multiplexer #(.select(5), .width(2), .enable("false")) multiplexer_3 (
    .in0(2'b00), .in1(2'b10), .in2(2'b10), .in3(2'b00), .in4(2'b01), .in5(2'b01), .in6(2'b00), .in7(2'b00),
    .in8(2'b00), .in9(2'b00), .in10(2'b00), .in11(2'b00), .in12(2'b00), .in13(2'b00), .in14(2'b00),
    .in15(2'b00), .in16(2'b00), .in17(2'b00), .in18(2'b00), .in19(2'b00), .in20(2'b00), .in21(2'b00),
    .in22(2'b00), .in23(2'b00), .in24(2'b00), .in25(2'b00), .in26(2'b00), .in27(2'b00), .in28(2'b00),
    .in29(2'b00), .in30(2'b00), .in31(2'b00), .out(multiplexer_3_out), .sel(IR_Code[4:0]));
  Multiplexer #(.select(3), .enable("false")) multiplexer_4 (
    .in0(1'b0), .in1(not_1_out), .in2(ZF), .in3(not_2_out), .in4(BAF), .in5(1'b0), .in6(1'b0), .in7(1'b0),
    .out(multiplexer_4_out), .sel(IR_Code[2:0]));
  not not_3 (not_3_out, IR_Code[0]);
  not not_4 (not_4_out, IR_Code[2]);
  not not_5 (not_5_out, IR_Code[3]);
  not not_6 (not_6_out, IR_Code[4]);
  not not_7 (not_7_out, IR_Code[1]);
  not not_8 (not_8_out, IR_Code[3]);
  not not_9 (not_9_out, IR_Code[4]);
  Multiplexer #(.select(5), .width(2), .enable("false")) multiplexer_5 (
    .in0(2'b00), .in1(2'b10), .in2(2'b10), .in3(2'b01), .in4(2'b10), .in5(2'b00), .in6(2'b00), .in7(2'b00),
    .in8(2'b00), .in9(2'b00), .in10(2'b00), .in11(2'b00), .in12(2'b00), .in13(2'b00), .in14(2'b00),
    .in15(2'b00), .in16(2'b00), .in17(2'b00), .in18(2'b00), .in19(2'b00), .in20(2'b00), .in21(2'b00),
    .in22(2'b00), .in23(2'b00), .in24(2'b00), .in25(2'b00), .in26(2'b00), .in27(2'b00), .in28(2'b00),
    .in29(2'b00), .in30(2'b00), .in31(2'b00), .out(multiplexer_5_out), .sel(IR_Code[4:0]));
  and and_1 (and_1_out, or_1_out, IR_Code[5]);
  not not_10 (not_10_out, IR_Code[0]);
  not not_11 (not_11_out, IR_Code[1]);
  not not_12 (not_12_out, IR_Code[2]);
  and and_2 (and_2_out, not_3_out, IR_Code[1], not_4_out, not_5_out, not_6_out, IR_Code[5]);
  and and_3 (and_3_out, IR_Code[0], not_7_out, IR_Code[2], not_8_out, not_9_out, IR_Code[5]);
  Multiplexer #(.enable("false")) multiplexer_6 (
    .in0(1'b1), .in1(multiplexer_2_out), .out(multiplexer_6_out), .sel(IR_Code[5]));
  Multiplexer #(.width(2), .enable("false")) multiplexer_7 (
    .in0(2'b00), .in1(multiplexer_3_out), .out(multiplexer_7_out), .sel(IR_Code[5]));
  Counter #(.width(2), .max('h3)) counter_1 (.Q(counter_1_q), .clk(clock_1_out));  // open: load, D, count, carry, clr
  Clock clock_1 (.out(clock_1_out));
  or or_2 (or_2_out, IR_Code[2], IR_Code[4]);
  and and_4 (and_4_out, or_2_out, IR_Code[5]);
  or or_3 (or_3_out, IR_Code[2], IR_Code[4]);
  and and_5 (and_5_out, and_1_out, multiplexer_4_out);
  and and_6 (and_6_out, not_10_out, not_11_out, not_12_out, IR_Code[3], IR_Code[4], IR_Code[5]);
  or or_4 (or_4_out, and_2_out, and_3_out);
  Multiplexer #(.width(2), .enable("false")) multiplexer_8 (
    .in0(2'b11), .in1(multiplexer_5_out), .out(multiplexer_8_out), .sel(IR_Code[5]));
  PC_Phase_Counter pc_phase_counter_1 (.x1(counter_1_q[1]), .a1(out_8[1]), .x2(counter_1_q[0]), .a2(out_8[0]));
  Multiplexer #(.select(2), .enable("false")) multiplexer_9 (
    .in0(1'b0), .in1(and_4_out), .in2(1'b0), .in3(1'b0), .out(imload), .sel(out_8));
  and and_7 (and_7_out, IR_Code[5], or_3_out);
  or or_5 (or_5_out, and_5_out, and_6_out);
  Multiplexer #(.select(2), .enable("false")) multiplexer_10 (
    .in0(1'b0), .in1(1'b0), .in2(or_4_out), .in3(1'b0), .out(readwrite), .sel(out_8));
  Multiplexer #(.select(2), .width(2), .enable("false")) multiplexer_11 (
    .in0(2'b00), .in1(2'b00), .in2(multiplexer_8_out), .in3(2'b00), .out(regsel), .sel(out_8));
  Multiplexer #(.select(2), .enable("false")) multiplexer_12 (
    .in0(1'b0), .in1(1'b0), .in2(multiplexer_6_out), .in3(1'b0), .out(dwrite), .sel(out_8));
  Multiplexer #(.select(2), .width(2), .enable("false")) multiplexer_13 (
    .in0(2'b00), .in1(2'b00), .in2(multiplexer_7_out), .in3(2'b00), .out(addrsel), .sel(out_8));
  Multiplexer #(.select(2), .enable("false")) multiplexer_14 (
    .in0(1'b1), .in1(and_7_out), .in2(or_5_out), .in3(1'b0), .out(pcload), .sel(out_8));
  Multiplexer #(.select(2), .enable("false")) multiplexer_15 (
    .in0(1'b1), .in1(1'b1), .in2(1'b0), .in3(1'b0), .out(pcsel), .sel(out_8));

  assign aluop = IR_Code[4:0];
  assign dregsel = IR_Reg[5:3];
  assign operation = IR_Code[4:0];
  assign sregsel = IR_Reg[2:0];

  // Other names for the same wires on the sheet: dreg[2:0] = IR_Reg[5:3]; bit0 = IR_Code[0];
  //   fullop[4:0] = IR_Code[4:0]; op2[2:0] = IR_Code[2:0]; bit1 = IR_Code[1]; bit2 = IR_Code[2]; bit3 = IR_Code[3];
  //   op1[2:0] = IR_Code[5:3]; bit4 = IR_Code[4]; aluop_t = IR_Code[5]; bit5 = IR_Code[5]; phase[1:0] = out_8;
  //   sreg[2:0] = IR_Reg[2:0]

  // Notes on the sheet:
  //   10
  //   01
  //   00
  //   10
  //   01
  //   00
  //   Get Operation
  //   Load IR
  //   00
  //   11
  //   Decoder
  //   Get Registers
  //   00
  //   Write to Destination register
  //   Set Registers
  //   Load Immed
  //   Load PC
  //   Read & Write
  //   Select Register
  //   Select Address
  //   Count 
  //   Phases
  //   Select PC
endmodule
